// Digital circuit 74LS161.dig as structural Verilog
module _74LS161 (
  input  CLK,
  input  A,
  input  B,
  input  C,
  input  D,
  input  nLD,
  input  nCLR,
  input  ENT,
  input  ENP,
  output QA,
  output QB,
  output QC,
  output QD,
  output RCO
);

  wire add_1_c_o, and_1_out;
  wire [3:0] add_1_s, multiplexer_1_out, multiplexer_2_out;

  Add #(.Bits(4)) add_1 (.a({QD, QC, QB, QA}), .b(4'b0001), .c_i(1'b0), .s(add_1_s), .c_o(add_1_c_o));
  and and_1 (and_1_out, ENP, ENT);
  Multiplexer #(.Bits(4)) multiplexer_1 (
    .sel(and_1_out), .in_0({QD, QC, QB, QA}), .in_1(add_1_s), .out(multiplexer_1_out));
  Multiplexer #(.Bits(4)) multiplexer_2 (
    .sel(nLD), .in_0({D, C, B, A}), .in_1(multiplexer_1_out), .out(multiplexer_2_out));
  D_FF_AS #(.Bits(4)) d_ff_as_1 (
    .Set(1'b0), .D(multiplexer_2_out), .C(CLK), .Clr(~nCLR), .Q({QD, QC, QB, QA}));  // open: nQ
  and and_2 (RCO, add_1_c_o, ENT);

  // Notes on the sheet:
  //   CLK: pin 2
  //   A: pin 3
  //   B: pin 4
  //   QA: pin 14
  //   C: pin 5
  //   D: pin 6
  //   nLD: pin 9
  //   nCLR: pin 1
  //   ENT: pin 10
  //   ENP: pin 7
  //   QB: pin 13
  //   QC: pin 12
  //   QD: pin 11
  //   RCO: pin 15
endmodule
