// Digital circuit 74LS174.dig as structural Verilog
module _74LS174 (
  input  D1,
  input  D2,
  input  D3,
  input  D4,
  input  D5,
  input  D6,
  input  CLK,
  input  nCL,
  output Q1,
  output Q2,
  output Q3,
  output Q4,
  output Q5,
  output Q6
);

  D_FF_AS #(.Bits(6)) d_ff_as_1 (
    .Set(1'b0), .D({D6, D5, D4, D3, D2, D1}), .C(CLK), .Clr(~nCL), .Q({Q6, Q5, Q4, Q3, Q2, Q1}));  // open: nQ

  // Notes on the sheet:
  //   D1: pin 3
  //   D2: pin 4
  //   D3: pin 6
  //   D4: pin 11
  //   D5: pin 13
  //   D6: pin 14
  //   CLK: pin 9
  //   nCL: pin 1
  //   Q1: pin 2
  //   Q2: pin 5
  //   Q3: pin 7
  //   Q4: pin 10
  //   Q5: pin 12
  //   Q6: pin 15
endmodule
