// Digital circuit 74LS238.dig as structural Verilog
module _74LS238 (
  input  A,
  input  B,
  input  C,
  input  G,
  input  nGB,
  input  nGA,
  output Y0,
  output Y1,
  output Y2,
  output Y3,
  output Y4,
  output Y5,
  output Y6,
  output Y7
);

  wire and_1_out;
  wire [2:0] delay_1_out;

  Delay #(.Bits(3)) delay_1 (.in({C, B, A}), .out(delay_1_out));
  and and_1 (and_1_out, G, ~nGB, ~nGA);  // And
  Demultiplexer #(.Selector_Bits(3)) demultiplexer_1 (
    .sel(delay_1_out), .in(and_1_out), .out_0(Y0), .out_1(Y1), .out_2(Y2), .out_3(Y3), .out_4(Y4),
    .out_5(Y5), .out_6(Y6), .out_7(Y7));

  // Notes on the sheet:
  //   A: pin 1
  //   B: pin 2
  //   C: pin 3
  //   G: pin 6
  //   nGB: pin 5
  //   nGA: pin 4
  //   Y0: pin 15
  //   Y1: pin 14
  //   Y2: pin 13
  //   Y3: pin 12
  //   Y4: pin 11
  //   Y5: pin 10
  //   Y6: pin 9
  //   Y7: pin 7
endmodule

/* Test case:
~GA ~GB G A B C Y0 Y1 Y2 Y3 Y4 Y5 Y6 Y7
1 X X X X X 0 0 0 0 0 0 0 0
X 1 X X X X 0 0 0 0 0 0 0 0
X X 0 X X X 0 0 0 0 0 0 0 0
0 0 1 0 0 0 1 0 0 0 0 0 0 0
0 0 1 1 0 0 0 1 0 0 0 0 0 0
0 0 1 0 1 0 0 0 1 0 0 0 0 0
0 0 1 1 1 0 0 0 0 1 0 0 0 0
0 0 1 0 0 1 0 0 0 0 1 0 0 0
0 0 1 1 0 1 0 0 0 0 0 1 0 0
0 0 1 0 1 1 0 0 0 0 0 0 1 0
0 0 1 1 1 1 0 0 0 0 0 0 0 1
*/
