// Digital circuit 74LS273.dig as structural Verilog
module _74LS273 (
  input  CP,
  input  nMR,
  input  D0,
  input  D1,
  input  D2,
  input  D3,
  input  D4,
  input  D5,
  input  D6,
  input  D7,
  output Q0,
  output Q1,
  output Q2,
  output Q3,
  output Q4,
  output Q5,
  output Q6,
  output Q7
);

  wire not_1_out;

  not not_1 (not_1_out, nMR);
  D_FF_AS #(.Bits(8)) d_ff_as_1 (
    .Set(1'b0), .D({D7, D6, D5, D4, D3, D2, D1, D0}), .C(CP), .Clr(not_1_out),
    .Q({Q7, Q6, Q5, Q4, Q3, Q2, Q1, Q0}));  // open: nQ

  // Notes on the sheet:
  //   CP: pin 11
  //   nMR: pin 1, default 1
  //   D0: pin 3
  //   D1: pin 4
  //   D2: pin 7
  //   D3: pin 8
  //   D4: pin 13
  //   D5: pin 14
  //   D6: pin 17
  //   D7: pin 18
  //   Q0: pin 2
  //   Q1: pin 5
  //   Q2: pin 6
  //   Q3: pin 9
  //   Q4: pin 12
  //   Q5: pin 15
  //   Q6: pin 16
  //   Q7: pin 19
endmodule

/* Test case:
~MR CP D0 Q0
 0  x  x  0
 1  0  1  0
 1  1  1  1
 1  0  x  1
 1  0  0  1
 1  1  0  0
 1  0  x  0
*/
