// Digital circuit 74LS283.dig as structural Verilog
module _74LS283 (
  input  A1,
  input  A2,
  input  A3,
  input  A4,
  input  B1,
  input  B2,
  input  B3,
  input  B4,
  input  C_in,
  output S1,
  output S2,
  output S3,
  output S4,
  output C_out
);

  Add #(.Bits(4)) add_1 (.a({A4, A3, A2, A1}), .b({B4, B3, B2, B1}), .c_i(C_in), .s({S4, S3, S2, S1}), .c_o(C_out));

  // Notes on the sheet:
  //   A1: pin 5
  //   A2: pin 3
  //   A3: pin 14
  //   S1: pin 4
  //   A4: pin 12
  //   B1: pin 6
  //   S2: pin 1
  //   S3: pin 13
  //   B2: pin 2
  //   B3: pin 15
  //   B4: pin 11
  //   C_in: pin 7
  //   S4: pin 10
  //   C_out: pin 9
endmodule

/* Test case:
# A complete test of all 512 possible additions
#

C_in   A4 A3 A2 A1   B4 B3 B2 B1  C_out S4 S3 S2 S1
loop(A,16)
  loop(B,16)
0    bits(4,A)     bits(4,B)    bits(5,A+B)
1    bits(4,A)     bits(4,B)    bits(5,A+B+1)
  end loop
end loop
*/
