// Digital circuit 74LS373.dig as structural Verilog
module _74LS373 (
  input  nOC,
  input  C,
  input  D0,
  input  D1,
  input  D2,
  input  D3,
  input  D4,
  input  D5,
  input  D6,
  input  D7,
  output Q0,
  output Q1,
  output Q2,
  output Q3,
  output Q4,
  output Q5,
  output Q6,
  output Q7
);

  wire and_1_out, and_2_out, and_3_out, and_4_out, and_5_out, and_6_out, and_7_out, and_8_out, and_9_out,
       and_10_out, and_11_out, and_12_out, and_13_out, and_14_out, and_15_out, and_16_out, rs_ff_as_1_q,
       rs_ff_as_2_q, rs_ff_as_3_q, rs_ff_as_4_q, rs_ff_as_5_q, rs_ff_as_6_q, rs_ff_as_7_q, rs_ff_as_8_q;

  and and_1 (and_1_out, C, D0);
  and and_2 (and_2_out, C, ~D0);  // And
  and and_3 (and_3_out, C, D1);
  and and_4 (and_4_out, C, ~D1);  // And
  and and_5 (and_5_out, C, D2);
  and and_6 (and_6_out, C, ~D2);  // And
  and and_7 (and_7_out, C, D3);
  and and_8 (and_8_out, C, ~D3);  // And
  and and_9 (and_9_out, C, D4);
  and and_10 (and_10_out, C, ~D4);  // And
  and and_11 (and_11_out, C, D5);
  and and_12 (and_12_out, C, ~D5);  // And
  and and_13 (and_13_out, C, D6);
  and and_14 (and_14_out, C, ~D6);  // And
  and and_15 (and_15_out, C, D7);
  and and_16 (and_16_out, C, ~D7);  // And
  RS_FF_AS rs_ff_as_1 (.S(and_1_out), .R(and_2_out), .Q(rs_ff_as_1_q));  // open: nQ
  RS_FF_AS rs_ff_as_2 (.S(and_3_out), .R(and_4_out), .Q(rs_ff_as_2_q));  // open: nQ
  RS_FF_AS rs_ff_as_3 (.S(and_5_out), .R(and_6_out), .Q(rs_ff_as_3_q));  // open: nQ
  RS_FF_AS rs_ff_as_4 (.S(and_7_out), .R(and_8_out), .Q(rs_ff_as_4_q));  // open: nQ
  RS_FF_AS rs_ff_as_5 (.S(and_9_out), .R(and_10_out), .Q(rs_ff_as_5_q));  // open: nQ
  RS_FF_AS rs_ff_as_6 (.S(and_11_out), .R(and_12_out), .Q(rs_ff_as_6_q));  // open: nQ
  RS_FF_AS rs_ff_as_7 (.S(and_13_out), .R(and_14_out), .Q(rs_ff_as_7_q));  // open: nQ
  RS_FF_AS rs_ff_as_8 (.S(and_15_out), .R(and_16_out), .Q(rs_ff_as_8_q));  // open: nQ
  assign Q0 = ~nOC ? rs_ff_as_1_q : 1'bz;  // DriverInvSel driverinvsel_1
  assign Q1 = ~nOC ? rs_ff_as_2_q : 1'bz;  // DriverInvSel driverinvsel_2
  assign Q2 = ~nOC ? rs_ff_as_3_q : 1'bz;  // DriverInvSel driverinvsel_3
  assign Q3 = ~nOC ? rs_ff_as_4_q : 1'bz;  // DriverInvSel driverinvsel_4
  assign Q4 = ~nOC ? rs_ff_as_5_q : 1'bz;  // DriverInvSel driverinvsel_5
  assign Q5 = ~nOC ? rs_ff_as_6_q : 1'bz;  // DriverInvSel driverinvsel_6
  assign Q6 = ~nOC ? rs_ff_as_7_q : 1'bz;  // DriverInvSel driverinvsel_7
  assign Q7 = ~nOC ? rs_ff_as_8_q : 1'bz;  // DriverInvSel driverinvsel_8

  // Notes on the sheet:
  //   Q0: pin 2
  //   Q1: pin 5
  //   Q2: pin 6
  //   Q3: pin 9
  //   nOC: pin 1, default 1
  //   C: pin 11
  //   Q4: pin 12
  //   Q5: pin 15
  //   Q6: pin 16
  //   Q7: pin 19
  //   D0: pin 3
  //   D1: pin 4
  //   D2: pin 7
  //   D3: pin 8
  //   D4: pin 13
  //   D5: pin 14
  //   D6: pin 17
  //   D7: pin 18
endmodule
