// Digital circuit Delay.dig as structural Verilog
module Delay (
  input  IN,
  input  RES,
  input  STP,
  output D1,
  output D2,
  output D3,
  output D4,
  output D5,
  output D6,
  output D7,
  output D8,
  output D9,
  output D10,
  output nD1,
  output nD2,
  output nD3,
  output nD4,
  output nD5,
  output nD6,
  output nD7,
  output nD8,
  output nD9,
  output nD10
);

  wire and_1_out, d_ff_as_1_nq, d_ff_as_1_q, d_ff_as_2_nq, d_ff_as_2_q, d_ff_as_3_nq, d_ff_as_3_q,
       d_ff_as_4_nq, d_ff_as_4_q, d_ff_as_5_nq, d_ff_as_5_q, d_ff_as_6_nq, d_ff_as_6_q, d_ff_as_7_nq,
       d_ff_as_7_q, d_ff_as_8_nq, d_ff_as_8_q, d_ff_as_9_nq, d_ff_as_9_q, d_ff_as_10_nq, d_ff_as_10_q,
       delay_1_out, delay_2_out, delay_3_out, delay_4_out, delay_5_out, delay_6_out, delay_7_out,
       delay_8_out, delay_9_out, delay_10_out, delay_11_out, delay_12_out, delay_13_out, delay_14_out,
       delay_15_out, delay_16_out, delay_17_out, delay_18_out, delay_19_out, delay_20_out, nand_1_out;

  D_FF_AS d_ff_as_1 (.Set(1'b0), .D(1'b1), .C(STP), .Clr(RES), .Q(d_ff_as_1_q), .nQ(d_ff_as_1_nq));
  D_FF_AS d_ff_as_2 (.Set(1'b0), .D(d_ff_as_1_q), .C(STP), .Clr(RES), .Q(d_ff_as_2_q), .nQ(d_ff_as_2_nq));
  D_FF_AS d_ff_as_3 (.Set(1'b0), .D(d_ff_as_2_q), .C(STP), .Clr(RES), .Q(d_ff_as_3_q), .nQ(d_ff_as_3_nq));
  D_FF_AS d_ff_as_4 (.Set(1'b0), .D(d_ff_as_3_q), .C(STP), .Clr(RES), .Q(d_ff_as_4_q), .nQ(d_ff_as_4_nq));
  D_FF_AS d_ff_as_5 (.Set(1'b0), .D(d_ff_as_4_q), .C(STP), .Clr(RES), .Q(d_ff_as_5_q), .nQ(d_ff_as_5_nq));
  D_FF_AS d_ff_as_6 (.Set(1'b0), .D(d_ff_as_5_q), .C(STP), .Clr(RES), .Q(d_ff_as_6_q), .nQ(d_ff_as_6_nq));
  D_FF_AS d_ff_as_7 (.Set(1'b0), .D(d_ff_as_6_q), .C(STP), .Clr(RES), .Q(d_ff_as_7_q), .nQ(d_ff_as_7_nq));
  D_FF_AS d_ff_as_8 (.Set(1'b0), .D(d_ff_as_7_q), .C(STP), .Clr(RES), .Q(d_ff_as_8_q), .nQ(d_ff_as_8_nq));
  D_FF_AS d_ff_as_9 (.Set(1'b0), .D(d_ff_as_8_q), .C(STP), .Clr(RES), .Q(d_ff_as_9_q), .nQ(d_ff_as_9_nq));
  D_FF_AS d_ff_as_10 (.Set(1'b0), .D(d_ff_as_9_q), .C(STP), .Clr(RES), .Q(d_ff_as_10_q), .nQ(d_ff_as_10_nq));
  and and_1 (and_1_out, IN, IN);
  nand nand_1 (nand_1_out, IN, IN);
  Delay #(.delayTime(10)) delay_1 (.in(and_1_out), .out(delay_1_out));
  Delay #(.delayTime(10)) delay_2 (.in(nand_1_out), .out(delay_2_out));
  or or_1 (D1, delay_1_out, d_ff_as_1_q);
  Delay #(.delayTime(10)) delay_3 (.in(delay_1_out), .out(delay_3_out));
  or or_2 (D2, delay_3_out, d_ff_as_2_q);
  Delay #(.delayTime(10)) delay_4 (.in(delay_3_out), .out(delay_4_out));
  or or_3 (D3, delay_4_out, d_ff_as_3_q);
  Delay #(.delayTime(10)) delay_5 (.in(delay_4_out), .out(delay_5_out));
  or or_4 (D4, delay_5_out, d_ff_as_4_q);
  Delay #(.delayTime(10)) delay_6 (.in(delay_5_out), .out(delay_6_out));
  or or_5 (D5, delay_6_out, d_ff_as_5_q);
  Delay #(.delayTime(10)) delay_7 (.in(delay_6_out), .out(delay_7_out));
  or or_6 (D6, delay_7_out, d_ff_as_6_q);
  Delay #(.delayTime(10)) delay_8 (.in(delay_7_out), .out(delay_8_out));
  or or_7 (D7, delay_8_out, d_ff_as_7_q);
  Delay #(.delayTime(10)) delay_9 (.in(delay_8_out), .out(delay_9_out));
  or or_8 (D8, delay_9_out, d_ff_as_8_q);
  Delay #(.delayTime(10)) delay_10 (.in(delay_9_out), .out(delay_10_out));
  or or_9 (D9, delay_10_out, d_ff_as_9_q);
  Delay #(.delayTime(10)) delay_11 (.in(delay_10_out), .out(delay_11_out));
  or or_10 (D10, delay_11_out, d_ff_as_10_q);
  and and_2 (nD1, delay_2_out, d_ff_as_1_nq);
  Delay #(.delayTime(10)) delay_12 (.in(delay_2_out), .out(delay_12_out));
  and and_3 (nD2, delay_12_out, d_ff_as_2_nq);
  Delay #(.delayTime(10)) delay_13 (.in(delay_12_out), .out(delay_13_out));
  and and_4 (nD3, delay_13_out, d_ff_as_3_nq);
  Delay #(.delayTime(10)) delay_14 (.in(delay_13_out), .out(delay_14_out));
  and and_5 (nD4, delay_14_out, d_ff_as_4_nq);
  Delay #(.delayTime(10)) delay_15 (.in(delay_14_out), .out(delay_15_out));
  and and_6 (nD5, delay_15_out, d_ff_as_5_nq);
  Delay #(.delayTime(10)) delay_16 (.in(delay_15_out), .out(delay_16_out));
  and and_7 (nD6, delay_16_out, d_ff_as_6_nq);
  Delay #(.delayTime(10)) delay_17 (.in(delay_16_out), .out(delay_17_out));
  and and_8 (nD7, delay_17_out, d_ff_as_7_nq);
  Delay #(.delayTime(10)) delay_18 (.in(delay_17_out), .out(delay_18_out));
  and and_9 (nD8, delay_18_out, d_ff_as_8_nq);
  Delay #(.delayTime(10)) delay_19 (.in(delay_18_out), .out(delay_19_out));
  and and_10 (nD9, delay_19_out, d_ff_as_9_nq);
  Delay #(.delayTime(10)) delay_20 (.in(delay_19_out), .out(delay_20_out));
  and and_11 (nD10, delay_20_out, d_ff_as_10_nq);
endmodule
