// Digital circuit NuPDP.dig as structural Verilog
module NuPDP (
  input  MAX,
  input  _100Hz,
  input  in_3,
  input  _1Hz,
  input  clk
);

  wire _0_out, _1_out, _2_out, _3_out, _4_out, _5_out, _6_out, _7_out, _74ls74_1__1nq, _74ls74_1__1q,
       _74ls74_2__1nq, _74ls74_2__2nq, _74ls74_3__1nq, _74ls74_3__1q, _74ls74_3__2q, _74ls74_4__1q,
       _74ls74_4__2q, _74ls85_3_p_eq_q, _74ls139_1_n1y0, _74ls139_1_n1y1, _74ls139_1_n1y2, _74ls139_1_n1y3,
       _74ls139_1_n2y0, _74ls139_1_n2y1, _74ls139_1_n2y2, _74ls139_1_n2y3, _74ls153_1__1y, _74ls153_1__2y,
       _74ls153_2__1y, _74ls153_3__1y, _74ls153_3__2y, _74ls153_4__1y, _74ls161_1_qa, _74ls161_1_qb,
       _74ls161_2_rco, _74ls161_3_rco, _74ls238_1_y1, _74ls238_1_y2, _74ls238_1_y3, _74ls238_1_y4,
       _74ls238_1_y5, _74ls238_1_y6, _74ls238_1_y7, _74ls238_2_y0, _74ls238_2_y1, _74ls238_2_y2,
       _74ls238_2_y3, _74ls238_2_y4, _74ls238_2_y5, _74ls238_2_y6, _74ls238_2_y7, _74ls238_3_y0,
       _74ls238_3_y1, _74ls238_3_y2, _74ls238_3_y3, _74ls238_3_y4, _74ls238_3_y5, _74ls238_4_y0,
       _74ls238_4_y1, _74ls238_4_y2, _74ls238_4_y3, _74ls247_1_na, _74ls247_1_nb, _74ls247_1_nc,
       _74ls247_1_nd, _74ls247_1_ne, _74ls247_1_nf, _74ls247_1_ng, _74ls273_2_q4, _74ls273_2_q5,
       _74ls273_2_q6, _74ls273_2_q7, _74ls273_9_q0, _74ls273_9_q1, _74ls273_9_q2, _74ls273_9_q3,
       _74ls273_9_q4, _74ls273_9_q5, _74ls273_9_q6, _74ls273_9_q7, _74ls273_10_q0, _74ls273_10_q1,
       _74ls273_10_q2, _74ls273_10_q3, _74ls283_1_c_out, _74ls283_1_s1, _74ls283_1_s2, _74ls283_1_s3,
       _74ls283_1_s4, _74ls283_2_c_out, _74ls283_2_s1, _74ls283_2_s2, _74ls283_2_s3, _74ls283_2_s4,
       _74ls283_3_s1, _74ls283_3_s2, _74ls283_3_s3, _74ls283_3_s4, _74ls283_4_c_out, _74ls283_5_c_out,
       _74ls393_1__1qa, _74ls393_1__1qb, _74ls393_1__1qc, _74ls393_1__1qd, _74ls393_1__2qa, _74ls393_1__2qb,
       _74ls393_1__2qc, _74ls393_1__2qd, _74ls393_2__1qb, _74ls393_2__1qc, _74ls393_2__2qa, _74ls393_2__2qb,
       _74ls541_6__7o, ACC11, aiFinished, ALU_Lin, ALU_Lout, AND, and_2_out, and_4_out, and_5_out, and_7_out,
       and_8_out, and_9_out, and_10_out, and_11_out, and_12_out, and_20_out, and_21_out, and_22_out,
       and_23_out, and_24_out, and_25_out, and_26_out, and_28_out, and_31_out, and_38_out, and_40_out,
       and_42_out, and_43_out, and_75_out, and_77_out, and_82_out, and_83_out, and_84_out, and_86_out,
       and_87_out, and_89_out, and_90_out, and_91_out, and_93_out, and_95_out, and_96_out, and_98_out,
       and_99_out, and_102_out, and_105_out, and_110_out, and_111_out, and_114_out, and_115_out, and_128_out,
       and_129_out, and_130_out, and_131_out, and_132_out, and_133_out, and_134_out, and_135_out,
       and_136_out, and_137_out, and_138_out, and_139_out, and_152_out, and_153_out, AND_TAD_d3, AND_TAD_d4,
       AND_TAD_d5, AND_TAD_d6, AND_TAD_p1, AND_TAD_p2, AND_TAD_p3, AND_TAD_p4, AND_TAD_p5, AND_TAD_p6,
       AND_TAD_p7, BP, BSW, C_out, CAF, CAF_6007, ckACC_2, ckACC_4, ckACC_5, ckACC_gtf, ckACC_iot1,
       ckACC_mop1, ckACC_mop2, ckBP, ckDBUStoABUS_0, ckDBUStoABUS_andtad, ckDBUStoABUS_dca, ckDBUStoABUS_isz,
       ckDBUStoABUS_jmp, ckDBUStoABUS_jms, ckDBUStoABUS_rim, ckIncDBUS__ai, ckIncDBUS__isz2, ckIncDBUS_isz1,
       ckIncPC_inc, ckIncPC_irq1, ckIncPC_jms1, ckIncPC_LoadIR, ckIR, ckIR_0, ckIR_irq, ckIR_LoadIR,
       ckIRQhandler, ckMQ_1, ckSetPC_0, ckSetPC_jmp, ckSetPC_jms, ckSwitch, CLA, CLA_1, CLA_2, CLA_3, CLA_4,
       CLK_t, CLL, clrPC_irq, CMA, CML, CODE_lsb, CODE_mid, CODE_msb, d_ff_as_1_q, d_ff_as_2_nq, d_ff_as_2_q,
       D_out, DCA, DCA_d1, DCA_d2, DCA_d3, DCA_d4, DCA_d5, DCA_p1, DCA_p2, DCA_p3, DCA_p4, DCA_p5, DCA_p7,
       delay_5_out, delay_7_out, delay_8_out, delay_9_out, delay_10_out, deposit_Rim, diodeforward_1_out,
       diodeforward_2_out, diodeforward_21_out, diodeforward_37_out, diodeforward_38_out,
       diodeforward_64_out, diodeforward_70_out, diodeforward_87_out, diodeforward_91_out,
       diodeforward_99_out, diodeforward_113_out, diodeforward_145_out, diodeforward_146_out,
       diodeforward_147_out, diodeforward_148_out, enACCclear_dca, enACCclear_iot1, enACCclear_mop3a,
       enACCtoDBUS_2, enACCtoDBUS_dca, enACCtoDBUS_tty, enALUadd, enALUand, enALUor_mop2, enALUtoACC_andtad,
       enALUtoACC_mop1, enALUtoACC_mop2, enDBUStoABUS_0, enDBUStoABUS_andtad, enDBUStoABUS_dca,
       enDBUStoABUS_rim, enIncToDBUS_ai, enIncToDBUS_isz1, enIncToDBUS_isz2, enINSTRtoABUS_ai,
       enINSTRtoABUS_andtad, enINSTRtoABUS_dca, enINSTRtoABUS_isz, enINSTRtoABUS_jmp, enINSTRtoABUS_jms,
       enIRQ, enKEYtoDBUS_0, enKEYtoDBUS_1, enKEYtoDBUS_3, enPCtoABUS_0, enPCtoABUS_irq, enPCtoABUS_LoadIR,
       enPCtoABUS_mop2, enPCtoDBUS_irq, enRAMtoDBUS_ai, enRAMtoDBUS_andtad, enRAMtoDBUS_dca, enRAMtoDBUS_isz,
       enRAMtoDBUS_jmp, enRAMtoDBUS_jms, fAccIsZero, fAutoinc, fDBUSisZero, fGIE, fIndirect, fIrqDly, fKBD,
       fPendInt, fPRN, fSkip, GTF_6004, H_out, HLT, I_out, IAC, IAC_carryout, iDone, iDone1, iDoneBeforeIRQ,
       ii, ii_dca, ii_iot, ii_isz, ii_jmp, ii_jms, ii_mop1, ii_mop2, ii_mop3a, INC1, INC1_iot, INC1_isz,
       INC1_mop2, INC1_mop3a, INC2, INC2_iot1, INC2_iot2, INC2_iot3, INC2_iot4, INC2_iot5, INC2_isz,
       INC2_mop2, INDIRECT, inhibitIR, INTE_nq, IOF_6002, ION_6001, IOT, IOT_CPU, IOT_d1, IOT_d2, IOT_d4,
       IOT_d5, IOT_d6, IOT_d7, IOT_d8, IOT_HISPEEDPUNCH, IOT_HISPEEDREADER, IOT_p2, IOT_p3, IOT_p4, IOT_p5,
       IOT_p6, IOT_p7, IOT_TTYPUNCH, IOT_TTYREADER, isCurrPage, ISZ, ISZ_ISZi_d1, ISZ_ISZi_d4, ISZ_ISZi_p1,
       ISZ_ISZi_p2, ISZ_ISZi_p3, JMP, JMP_JMPi_d2, JMP_JMPi_d3, JMP_JMPi_d4, JMP_JMPi_d5, JMP_JMPi_d6,
       JMP_JMPi_p1, JMP_JMPi_p2, JMP_JMPi_p3, JMP_JMPi_p4, JMP_JMPi_p5, JMP_JMPi_p6, JMP_JMPi_p7, JMS,
       JMS_JMSi_d2, JMS_JMSi_d3, JMS_JMSi_d4, JMS_JMSi_d6, JMS_JMSi_d7, JMS_JMSi_d8, JMS_JMSi_p1,
       JMS_JMSi_p2, JMS_JMSi_p5, JMS_JMSi_p6, JMS_JMSi_p7, KCC_6032, KCF_6030, KIE, KIE_6035, KRB, KRB_6036,
       KRS_6034, KSF_6031, L_out, LINK, M_out, MOP1, MOP1_d4, MOP1_d5, MOP1_d6, MOP1_d7, MOP1_d8, MOP1_p1,
       MOP1_p2, MOP1_p3, MOP1_p4, MOP1_p5, MOP1_p6, MOP1_p7, MOP2, MOP2_d2, MOP2_d4, MOP2_d5, MOP2_d7,
       MOP2_d8, MOP2_p1, MOP2_p3, MOP2_p4, MOP2_p5, MOP2_p6, MOP2_p7, MOP3, MOP3_d1, MOP3_d2, MOP3_d3,
       MOP3_d5, MOP3_d6, MOP3_d7, MOP3_p2, MOP3_p3, MOP3_p4, MOP3_p5, MOP3_p6, MOP3_p7, MQA, MQL, nand_1_out,
       nand_2_out, nand_3_out, nand_4_out, nand_5_out, nand_6_out, nor_1_out, nor_2_out, not_1_out,
       not_2_out, not_3_out, not_4_out, not_5_out, not_6_out, not_7_out, not_8_out, not_9_out, not_10_out,
       not_13_out, not_14_out, not_15_out, not_16_out, not_18_out, not_21_out, not_23_out, not_24_out,
       not_25_out, not_26_out, not_27_out, not_28_out, not_29_out, not_30_out, not_31_out, not_32_out,
       not_33_out, not_34_out, not_35_out, not_36_out, not_37_out, not_38_out, not_39_out, not_40_out,
       not_41_out, not_42_out, not_43_out, not_44_out, not_45_out, not_46_out, not_47_out, not_48_out,
       not_49_out, not_50_out, not_52_out, not_54_out, not_56_out, not_57_out, not_58_out, not_59_out,
       not_60_out, not_61_out, not_62_out, nRESET, oneshot_1_o, oneshot_2_o, oneshot_3_o, oneshot_4_o,
       oneshot_5_o, oneshot_6_o, oneshot_7_o, oneshot_8_o, oneshot_10_o, oneshot_11_o, oneshot_12_o,
       oneshot_13_o, oneshot_14_o, or_1_out, or_3_out, or_4_out, or_5_out, or_6_out, or_7_out, or_8_out,
       or_9_out, or_10_out, or_11_out, or_13_out, or_14_out, or_15_out, or_16_out, or_17_out, or_18_out,
       or_19_out, or_20_out, or_21_out, or_25_out, or_26_out, or_27_out, or_28_out, or_29_out, or_30_out,
       or_35_out, or_36_out, or_37_out, or_46_out, or_47_out, or_49_out, or_50_out, or_51_out, or_52_out,
       or_53_out, or_55_out, or_56_out, or_57_out, or_58_out, or_60_out, or_61_out, or_62_out, or_63_out,
       or_64_out, or_65_out, or_66_out, or_67_out, or_68_out, or_69_out, or_70_out, or_71_out, or_72_out,
       or_85_out, or_86_out, or_87_out, or_88_out, or_89_out, or_90_out, or_91_out, or_92_out, P_out, PC_rim,
       pulldown_7_out, pulldown_12_out, pulldown_13_out, R_out, RESET, rs_ff_as_1_nq, rs_ff_as_3_q,
       rs_ff_as_4_q, RTF_INTEclr, RTF_INTEset, RTF_linkClr, RTF_linkSet, S_out, sequencer_1_d2,
       sequencer_1_d3, sequencer_1_d4, sequencer_1_d5, sequencer_1_d6, sequencer_1_d7, sequencer_1_p3,
       sequencer_1_p4, sequencer_1_p5, sequencer_1_p6, sequencer_1_p7, sequencer_2_d1, sequencer_2_d2,
       sequencer_2_d3, sequencer_2_d5, sequencer_2_d6, sequencer_2_d7, sequencer_2_p2, sequencer_2_p4,
       sequencer_2_p7, STOP, t_ff_1_q, T_out, tty_1_rxavail, tty_1_txdone, TTY_IE_q, weRAM_ai, weRAM_dca,
       weRAM_irq, weRAM_rim, xor_2_out, xor_3_out, xor_4_out, xor_5_out, xor_6_out, xor_7_out, xor_8_out,
       xor_9_out, xor_10_out, xor_11_out, xor_12_out, xor_13_out, xor_14_out, ZEROPAGE;
  wire [2:0] _74ls85_1_p_lt_q, _74ls85_2_p_lt_q;
  wire [3:0] _74ls541_6__3o;
  wire [5:0] _74ls174_1_q6, _74ls174_2_q6, L_PRN;
  wire [5:2] L_IRQ;
  wire [7:0] _74ls541_5__7o;
  wire [7:1] L_CPU;
  wire [8:1] L_OPR2;
  wire [10:0] ACCC;
  wire [10:1] L_OPR1;
  wire [10:3] L_GEN;
  wire [11:0] _74ls283_5_s4, ABUS, ALU_xout, and_127_out, and_151_out, BPaddress, IR, IRA, MQ, OBUS,
       or_84_out, PC, ramspy_1_o, ramspy_2_o, switch;
  wire [12:0] L_OPR3;
  wire [19:0] counter_1_out, d_ff_1_q;
  wire [24:0] DAW;
  wire [50:0] CharRom3x_d;

  Button L (.out(L_out));
  OneShot oneshot_1 (.i(L_out), .o(oneshot_1_o));
  or or_1 (or_1_out, RESET, _74ls238_3_y5);
  not not_1 (not_1_out, oneshot_1_o);
  not not_2 (not_2_out, or_1_out);
  _74LS74 _74ls74_1 (
    ._1nSD(not_1_out), ._1D(1'b0), ._1CP(1'b0), ._1nRD(not_2_out), ._2nSD(1'b1), ._2D(1'b0), ._2CP(1'b0),
    ._2nRD(1'b1), ._1Q(_74ls74_1__1q), ._1nQ(_74ls74_1__1nq));  // open: _2Q, _2nQ
  _74LS393 _74ls393_1 (
    ._1A(_100Hz), ._1CL(_74ls74_1__1nq), ._2A(_74ls393_1__1qd), ._2CL(_74ls74_1__1nq),
    ._1QA(_74ls393_1__1qa), ._1QB(_74ls393_1__1qb), ._1QC(_74ls393_1__1qc), ._1QD(_74ls393_1__1qd),
    ._2QA(_74ls393_1__2qa), ._2QB(_74ls393_1__2qb), ._2QC(_74ls393_1__2qc), ._2QD(_74ls393_1__2qd));
  _74LS238 _74ls238_1 (
    .A(_74ls393_1__1qd), .B(_74ls393_1__2qa), .C(_74ls393_1__2qb), .G(1'b1), .nGB(_74ls393_1__2qc),
    .nGA(_74ls393_1__2qd), .Y1(_74ls238_1_y1), .Y2(_74ls238_1_y2), .Y3(_74ls238_1_y3), .Y4(_74ls238_1_y4),
    .Y5(_74ls238_1_y5), .Y6(_74ls238_1_y6), .Y7(_74ls238_1_y7));  // open: Y0
  _74LS238 _74ls238_2 (
    .A(_74ls393_1__1qd), .B(_74ls393_1__2qa), .C(_74ls393_1__2qb), .G(_74ls393_1__2qc),
    .nGB(_74ls393_1__2qd), .nGA(1'b0), .Y0(_74ls238_2_y0), .Y1(_74ls238_2_y1), .Y2(_74ls238_2_y2),
    .Y3(_74ls238_2_y3), .Y4(_74ls238_2_y4), .Y5(_74ls238_2_y5), .Y6(_74ls238_2_y6), .Y7(_74ls238_2_y7));
  _74LS238 _74ls238_3 (
    .A(_74ls393_1__1qd), .B(_74ls393_1__2qa), .C(_74ls393_1__2qb), .G(_74ls393_1__2qd),
    .nGB(_74ls393_1__2qc), .nGA(1'b0), .Y0(_74ls238_3_y0), .Y1(_74ls238_3_y1), .Y2(_74ls238_3_y2),
    .Y3(_74ls238_3_y3), .Y4(_74ls238_3_y4), .Y5(_74ls238_3_y5));  // open: Y6, Y7
  and and_1 (deposit_Rim, diodeforward_2_out, _74ls393_1__1qc);
  and and_2 (and_2_out, _74ls74_1__1q, _100Hz);
  and and_3 (PC_rim, diodeforward_1_out, _74ls393_1__1qc);
  DiodeForward diodeforward_1 (.in(_74ls238_1_y1), .out(diodeforward_1_out));
  DiodeForward diodeforward_2 (.in(_74ls238_1_y2), .out(diodeforward_2_out));
  DiodeForward diodeforward_3 (.in(_74ls238_1_y3), .out(diodeforward_2_out));
  DiodeForward diodeforward_4 (.in(_74ls238_1_y4), .out(diodeforward_2_out));
  DiodeForward diodeforward_5 (.in(_74ls238_1_y5), .out(diodeforward_2_out));
  DiodeForward diodeforward_6 (.in(_74ls238_1_y6), .out(diodeforward_2_out));
  DiodeForward diodeforward_7 (.in(_74ls238_1_y7), .out(diodeforward_2_out));
  DiodeForward diodeforward_8 (.in(_74ls238_2_y0), .out(diodeforward_2_out));
  DiodeForward diodeforward_9 (.in(_74ls238_2_y1), .out(diodeforward_2_out));
  DiodeForward diodeforward_10 (.in(_74ls238_2_y2), .out(diodeforward_2_out));
  DiodeForward diodeforward_11 (.in(_74ls238_2_y3), .out(diodeforward_2_out));
  DiodeForward diodeforward_12 (.in(_74ls238_2_y4), .out(diodeforward_2_out));
  DiodeForward diodeforward_13 (.in(_74ls238_2_y5), .out(diodeforward_2_out));
  DiodeForward diodeforward_14 (.in(_74ls238_2_y6), .out(diodeforward_2_out));
  DiodeForward diodeforward_15 (.in(_74ls238_2_y7), .out(diodeforward_2_out));
  DiodeForward diodeforward_16 (.in(_74ls238_3_y0), .out(diodeforward_2_out));
  DiodeForward diodeforward_17 (.in(_74ls238_3_y1), .out(diodeforward_2_out));
  DiodeForward diodeforward_18 (.in(_74ls238_3_y2), .out(diodeforward_2_out));
  DiodeForward diodeforward_19 (.in(_74ls238_3_y3), .out(diodeforward_2_out));
  DiodeForward diodeforward_20 (.in(_74ls238_3_y4), .out(diodeforward_1_out));
  PullDown pulldown_1 (.out(diodeforward_2_out));
  PullDown pulldown_2 (.out(diodeforward_1_out));
  DiodeForward diodeforward_21 (.in(_74ls238_1_y1), .out(diodeforward_21_out));
  DiodeForward diodeforward_22 (.in(_74ls238_1_y2), .out(diodeforward_21_out));
  DiodeForward diodeforward_23 (.in(_74ls238_1_y3), .out(diodeforward_21_out));
  DiodeForward diodeforward_24 (.in(_74ls238_1_y4), .out(diodeforward_21_out));
  DiodeForward diodeforward_25 (.in(_74ls238_1_y5), .out(diodeforward_21_out));
  DiodeForward diodeforward_26 (.in(_74ls238_1_y6), .out(diodeforward_21_out));
  DiodeForward diodeforward_27 (.in(_74ls238_1_y7), .out(diodeforward_21_out));
  DiodeForward diodeforward_28 (.in(_74ls238_2_y0), .out(diodeforward_21_out));
  DiodeForward diodeforward_29 (.in(_74ls238_2_y1), .out(diodeforward_21_out));
  DiodeForward diodeforward_30 (.in(_74ls238_2_y2), .out(diodeforward_21_out));
  DiodeForward diodeforward_31 (.in(_74ls238_2_y3), .out(diodeforward_21_out));
  DiodeForward diodeforward_32 (.in(_74ls238_2_y4), .out(diodeforward_21_out));
  DiodeForward diodeforward_33 (.in(_74ls238_2_y5), .out(diodeforward_21_out));
  DiodeForward diodeforward_34 (.in(_74ls238_2_y6), .out(diodeforward_21_out));
  DiodeForward diodeforward_35 (.in(_74ls238_3_y1), .out(diodeforward_21_out));
  DiodeForward diodeforward_36 (.in(_74ls238_3_y4), .out(diodeforward_21_out));
  PullDown pulldown_3 (.out(diodeforward_21_out));
  DiodeForward diodeforward_37 (.in(_74ls238_1_y1), .out(diodeforward_37_out));
  DiodeForward diodeforward_38 (.in(_74ls238_1_y1), .out(diodeforward_38_out));
  DiodeForward diodeforward_39 (.in(_74ls238_1_y2), .out(diodeforward_37_out));
  DiodeForward diodeforward_40 (.in(_74ls238_1_y3), .out(diodeforward_37_out));
  DiodeForward diodeforward_41 (.in(_74ls238_1_y4), .out(diodeforward_38_out));
  DiodeForward diodeforward_42 (.in(_74ls238_1_y5), .out(diodeforward_37_out));
  DiodeForward diodeforward_43 (.in(_74ls238_1_y6), .out(diodeforward_37_out));
  DiodeForward diodeforward_44 (.in(_74ls238_1_y6), .out(diodeforward_38_out));
  DiodeForward diodeforward_45 (.in(_74ls238_1_y7), .out(diodeforward_37_out));
  DiodeForward diodeforward_46 (.in(_74ls238_1_y7), .out(diodeforward_38_out));
  DiodeForward diodeforward_47 (.in(_74ls238_2_y0), .out(diodeforward_37_out));
  DiodeForward diodeforward_48 (.in(_74ls238_2_y0), .out(diodeforward_38_out));
  DiodeForward diodeforward_49 (.in(_74ls238_2_y1), .out(diodeforward_38_out));
  DiodeForward diodeforward_50 (.in(_74ls238_2_y2), .out(diodeforward_38_out));
  DiodeForward diodeforward_51 (.in(_74ls238_2_y2), .out(diodeforward_37_out));
  DiodeForward diodeforward_52 (.in(_74ls238_2_y3), .out(diodeforward_37_out));
  DiodeForward diodeforward_53 (.in(_74ls238_2_y4), .out(diodeforward_38_out));
  DiodeForward diodeforward_54 (.in(_74ls238_2_y5), .out(diodeforward_37_out));
  DiodeForward diodeforward_55 (.in(_74ls238_2_y6), .out(diodeforward_37_out));
  DiodeForward diodeforward_56 (.in(_74ls238_2_y6), .out(diodeforward_38_out));
  DiodeForward diodeforward_57 (.in(_74ls238_2_y7), .out(diodeforward_37_out));
  DiodeForward diodeforward_58 (.in(_74ls238_2_y7), .out(diodeforward_38_out));
  DiodeForward diodeforward_59 (.in(_74ls238_3_y0), .out(diodeforward_37_out));
  DiodeForward diodeforward_60 (.in(_74ls238_3_y0), .out(diodeforward_38_out));
  DiodeForward diodeforward_61 (.in(_74ls238_3_y1), .out(diodeforward_38_out));
  DiodeForward diodeforward_62 (.in(_74ls238_3_y4), .out(diodeforward_37_out));
  DiodeForward diodeforward_63 (.in(_74ls238_3_y4), .out(diodeforward_38_out));
  PullDown pulldown_4 (.out(diodeforward_37_out));
  PullDown pulldown_5 (.out(diodeforward_38_out));
  DiodeForward diodeforward_64 (.in(_74ls238_1_y1), .out(diodeforward_64_out));
  DiodeForward diodeforward_65 (.in(_74ls238_2_y0), .out(diodeforward_64_out));
  DiodeForward diodeforward_66 (.in(_74ls238_2_y6), .out(diodeforward_64_out));
  DiodeForward diodeforward_67 (.in(_74ls238_2_y7), .out(diodeforward_64_out));
  DiodeForward diodeforward_68 (.in(_74ls238_3_y4), .out(diodeforward_64_out));
  PullDown pulldown_6 (.out(diodeforward_64_out));
  PullDown pulldown_7 (.out(pulldown_7_out));
  DiodeForward diodeforward_69 (.in(_74ls238_1_y1), .out(pulldown_7_out));
  DiodeForward diodeforward_70 (.in(_74ls238_1_y1), .out(diodeforward_70_out));
  DiodeForward diodeforward_71 (.in(_74ls238_1_y4), .out(pulldown_7_out));
  DiodeForward diodeforward_72 (.in(_74ls238_1_y4), .out(diodeforward_70_out));
  DiodeForward diodeforward_73 (.in(_74ls238_1_y6), .out(diodeforward_70_out));
  DiodeForward diodeforward_74 (.in(_74ls238_2_y0), .out(diodeforward_70_out));
  DiodeForward diodeforward_75 (.in(_74ls238_2_y1), .out(pulldown_7_out));
  DiodeForward diodeforward_76 (.in(_74ls238_2_y1), .out(diodeforward_70_out));
  DiodeForward diodeforward_77 (.in(_74ls238_2_y4), .out(pulldown_7_out));
  DiodeForward diodeforward_78 (.in(_74ls238_2_y4), .out(diodeforward_70_out));
  DiodeForward diodeforward_79 (.in(_74ls238_2_y7), .out(pulldown_7_out));
  DiodeForward diodeforward_80 (.in(_74ls238_2_y7), .out(diodeforward_70_out));
  DiodeForward diodeforward_81 (.in(_74ls238_3_y0), .out(pulldown_7_out));
  DiodeForward diodeforward_82 (.in(_74ls238_3_y0), .out(diodeforward_70_out));
  DiodeForward diodeforward_83 (.in(_74ls238_3_y1), .out(pulldown_7_out));
  DiodeForward diodeforward_84 (.in(_74ls238_3_y1), .out(diodeforward_70_out));
  DiodeForward diodeforward_85 (.in(_74ls238_3_y4), .out(pulldown_7_out));
  DiodeForward diodeforward_86 (.in(_74ls238_3_y4), .out(diodeforward_70_out));
  PullDown pulldown_8 (.out(diodeforward_70_out));
  DiodeForward diodeforward_87 (.in(_74ls238_1_y1), .out(diodeforward_87_out));
  DiodeForward diodeforward_88 (.in(_74ls238_1_y4), .out(diodeforward_87_out));
  DiodeForward diodeforward_89 (.in(_74ls238_2_y1), .out(diodeforward_87_out));
  DiodeForward diodeforward_90 (.in(_74ls238_2_y4), .out(diodeforward_87_out));
  DiodeForward diodeforward_91 (.in(_74ls238_2_y4), .out(diodeforward_91_out));
  DiodeForward diodeforward_92 (.in(_74ls238_2_y6), .out(diodeforward_91_out));
  DiodeForward diodeforward_93 (.in(_74ls238_2_y7), .out(diodeforward_87_out));
  DiodeForward diodeforward_94 (.in(_74ls238_2_y7), .out(diodeforward_91_out));
  DiodeForward diodeforward_95 (.in(_74ls238_3_y0), .out(diodeforward_87_out));
  DiodeForward diodeforward_96 (.in(_74ls238_3_y0), .out(diodeforward_91_out));
  DiodeForward diodeforward_97 (.in(_74ls238_3_y1), .out(diodeforward_87_out));
  DiodeForward diodeforward_98 (.in(_74ls238_3_y4), .out(diodeforward_87_out));
  PullDown pulldown_9 (.out(diodeforward_91_out));
  PullDown pulldown_10 (.out(diodeforward_87_out));
  DiodeForward diodeforward_99 (.in(_74ls238_1_y1), .out(diodeforward_99_out));
  DiodeForward diodeforward_100 (.in(_74ls238_1_y2), .out(diodeforward_99_out));
  DiodeForward diodeforward_101 (.in(_74ls238_1_y3), .out(diodeforward_99_out));
  DiodeForward diodeforward_102 (.in(_74ls238_1_y4), .out(diodeforward_99_out));
  DiodeForward diodeforward_103 (.in(_74ls238_1_y5), .out(diodeforward_99_out));
  DiodeForward diodeforward_104 (.in(_74ls238_2_y0), .out(diodeforward_99_out));
  DiodeForward diodeforward_105 (.in(_74ls238_2_y1), .out(diodeforward_99_out));
  DiodeForward diodeforward_106 (.in(_74ls238_2_y3), .out(diodeforward_99_out));
  DiodeForward diodeforward_107 (.in(_74ls238_2_y5), .out(diodeforward_99_out));
  DiodeForward diodeforward_108 (.in(_74ls238_2_y7), .out(diodeforward_99_out));
  DiodeForward diodeforward_109 (.in(_74ls238_3_y0), .out(diodeforward_99_out));
  DiodeForward diodeforward_110 (.in(_74ls238_3_y1), .out(diodeforward_99_out));
  DiodeForward diodeforward_111 (.in(_74ls238_3_y4), .out(diodeforward_99_out));
  PullDown pulldown_11 (.out(diodeforward_99_out));
  PullDown pulldown_12 (.out(pulldown_12_out));
  DiodeForward diodeforward_112 (.in(_74ls238_1_y1), .out(pulldown_12_out));
  DiodeForward diodeforward_113 (.in(_74ls238_1_y1), .out(diodeforward_113_out));
  DiodeForward diodeforward_114 (.in(_74ls238_1_y2), .out(pulldown_12_out));
  DiodeForward diodeforward_115 (.in(_74ls238_1_y4), .out(pulldown_12_out));
  DiodeForward diodeforward_116 (.in(_74ls238_1_y4), .out(diodeforward_113_out));
  DiodeForward diodeforward_117 (.in(_74ls238_1_y5), .out(pulldown_12_out));
  DiodeForward diodeforward_118 (.in(_74ls238_1_y5), .out(diodeforward_113_out));
  DiodeForward diodeforward_119 (.in(_74ls238_1_y6), .out(pulldown_12_out));
  DiodeForward diodeforward_120 (.in(_74ls238_1_y6), .out(diodeforward_113_out));
  DiodeForward diodeforward_121 (.in(_74ls238_1_y7), .out(pulldown_12_out));
  DiodeForward diodeforward_122 (.in(_74ls238_1_y7), .out(diodeforward_113_out));
  DiodeForward diodeforward_123 (.in(_74ls238_2_y1), .out(pulldown_12_out));
  DiodeForward diodeforward_124 (.in(_74ls238_2_y1), .out(diodeforward_113_out));
  DiodeForward diodeforward_125 (.in(_74ls238_2_y2), .out(pulldown_12_out));
  DiodeForward diodeforward_126 (.in(_74ls238_2_y2), .out(diodeforward_113_out));
  DiodeForward diodeforward_127 (.in(_74ls238_2_y4), .out(pulldown_12_out));
  DiodeForward diodeforward_128 (.in(_74ls238_2_y4), .out(diodeforward_113_out));
  DiodeForward diodeforward_129 (.in(_74ls238_2_y5), .out(pulldown_12_out));
  DiodeForward diodeforward_130 (.in(_74ls238_2_y5), .out(diodeforward_113_out));
  DiodeForward diodeforward_131 (.in(_74ls238_2_y7), .out(pulldown_12_out));
  DiodeForward diodeforward_132 (.in(_74ls238_2_y7), .out(diodeforward_113_out));
  DiodeForward diodeforward_133 (.in(_74ls238_3_y0), .out(pulldown_12_out));
  DiodeForward diodeforward_134 (.in(_74ls238_3_y0), .out(diodeforward_113_out));
  DiodeForward diodeforward_135 (.in(_74ls238_3_y1), .out(pulldown_12_out));
  DiodeForward diodeforward_136 (.in(_74ls238_3_y1), .out(diodeforward_113_out));
  DiodeForward diodeforward_137 (.in(_74ls238_3_y4), .out(pulldown_12_out));
  DiodeForward diodeforward_138 (.in(_74ls238_3_y4), .out(diodeforward_113_out));
  PullDown pulldown_13 (.out(pulldown_13_out));
  PullDown pulldown_14 (.out(diodeforward_113_out));
  DiodeForward diodeforward_139 (.in(_74ls238_1_y3), .out(pulldown_13_out));
  DiodeForward diodeforward_140 (.in(_74ls238_1_y4), .out(pulldown_13_out));
  DiodeForward diodeforward_141 (.in(_74ls238_2_y1), .out(pulldown_13_out));
  DiodeForward diodeforward_142 (.in(_74ls238_2_y3), .out(pulldown_13_out));
  DiodeForward diodeforward_143 (.in(_74ls238_2_y4), .out(pulldown_13_out));
  DiodeForward diodeforward_144 (.in(_74ls238_3_y1), .out(pulldown_13_out));
  _74LS153 _74ls153_1 (
    ._1G(and_2_out), ._1C0(diodeforward_38_out), ._1C1(diodeforward_70_out), ._1C2(diodeforward_99_out),
    ._1C3(pulldown_13_out), ._2G(and_2_out), ._2C0(diodeforward_37_out), ._2C1(pulldown_7_out),
    ._2C2(diodeforward_91_out), ._2C3(diodeforward_113_out), .A(_74ls393_1__1qa), .B(_74ls393_1__1qb),
    ._1Y(_74ls153_1__1y), ._2Y(_74ls153_1__2y));
  _74LS153 _74ls153_2 (
    ._1G(and_2_out), ._1C0(diodeforward_21_out), ._1C1(diodeforward_64_out), ._1C2(diodeforward_87_out),
    ._1C3(pulldown_12_out), ._2G(1'b0), ._2C0(1'b0), ._2C1(1'b0), ._2C2(1'b0), ._2C3(1'b0),
    .A(_74ls393_1__1qa), .B(_74ls393_1__1qb), ._1Y(_74ls153_2__1y));  // open: _2Y
  DiodeForward diodeforward_145 (.in(and_2_out), .out(diodeforward_145_out));
  DiodeForward diodeforward_146 (.in(_74ls153_1__1y), .out(diodeforward_146_out));
  DiodeForward diodeforward_147 (.in(_74ls153_1__2y), .out(diodeforward_147_out));
  DiodeForward diodeforward_148 (.in(_74ls153_2__1y), .out(diodeforward_148_out));
  // Probe on ABUS
  PullDown #(.Bits(12)) pulldown_15 (.out(ABUS));
  or or_2 (DAW[24], weRAM_dca, enIncToDBUS_isz1, enIncToDBUS_isz2, weRAM_rim, weRAM_irq, ckIncPC_jms1, weRAM_ai);
  or or_3 (or_3_out, enPCtoABUS_0, enPCtoABUS_LoadIR, enRAMtoDBUS_jmp, enRAMtoDBUS_jms, enPCtoABUS_irq, enRAMtoDBUS_andtad, enRAMtoDBUS_ai, enRAMtoDBUS_isz, enRAMtoDBUS_dca);
  or or_4 (or_4_out, enIncToDBUS_isz1, enIncToDBUS_isz2, enIncToDBUS_ai);
  or or_5 (or_5_out, ckIncDBUS_isz1, ckIncDBUS__isz2, ckIncDBUS__ai);
  _74LS273 _74ls273_1 (
    .CP(ckBP), .nMR(nRESET), .D0(DAW[0]), .D1(DAW[1]), .D2(DAW[2]), .D3(DAW[3]), .D4(DAW[4]), .D5(DAW[5]),
    .D6(DAW[6]), .D7(DAW[7]), .Q0(BPaddress[0]), .Q1(BPaddress[1]), .Q2(BPaddress[2]), .Q3(BPaddress[3]),
    .Q4(BPaddress[4]), .Q5(BPaddress[5]), .Q6(BPaddress[6]), .Q7(BPaddress[7]));
  _74LS273 _74ls273_2 (
    .CP(ckBP), .nMR(nRESET), .D0(DAW[8]), .D1(DAW[9]), .D2(DAW[10]), .D3(DAW[11]), .D4(1'b0), .D5(1'b0),
    .D6(1'b0), .D7(1'b0), .Q0(BPaddress[8]), .Q1(BPaddress[9]), .Q2(BPaddress[10]), .Q3(BPaddress[11]),
    .Q4(_74ls273_2_q4), .Q5(_74ls273_2_q5), .Q6(_74ls273_2_q6), .Q7(_74ls273_2_q7));
  not not_3 (not_3_out, DAW[24]);
  not not_4 (not_4_out, or_3_out);
  not not_5 (not_5_out, or_4_out);
  _74LS283 _74ls283_1 (
    .A1(DAW[0]), .A2(DAW[1]), .A3(DAW[2]), .A4(DAW[3]), .B1(1'b0), .B2(1'b0), .B3(1'b0), .B4(1'b0),
    .S1(_74ls283_1_s1), .S2(_74ls283_1_s2), .S3(_74ls283_1_s3), .S4(_74ls283_1_s4), .C_in(1'b1),
    .C_out(_74ls283_1_c_out));
  _74LS283 _74ls283_2 (
    .A1(DAW[4]), .A2(DAW[5]), .A3(DAW[6]), .A4(DAW[7]), .B1(1'b0), .B2(1'b0), .B3(1'b0), .B4(1'b0),
    .S1(_74ls283_2_s1), .S2(_74ls283_2_s2), .S3(_74ls283_2_s3), .S4(_74ls283_2_s4), .C_in(_74ls283_1_c_out),
    .C_out(_74ls283_2_c_out));
  _74LS283 _74ls283_3 (
    .A1(DAW[8]), .A2(DAW[9]), .A3(DAW[10]), .A4(DAW[11]), .B1(1'b0), .B2(1'b0), .B3(1'b0), .B4(1'b0),
    .S1(_74ls283_3_s1), .S2(_74ls283_3_s2), .S3(_74ls283_3_s3), .S4(_74ls283_3_s4), .C_in(_74ls283_2_c_out));  // open: C_out
  Button _0 (.out(_0_out));
  DiodeForward diodeforward_149 (.in(_0_out), .out(diodeforward_145_out));
  Button _1 (.out(_1_out));
  DiodeForward diodeforward_150 (.in(_1_out), .out(diodeforward_145_out));
  Button _2 (.out(_2_out));
  DiodeForward diodeforward_151 (.in(_2_out), .out(diodeforward_145_out));
  Button _3 (.out(_3_out));
  DiodeForward diodeforward_152 (.in(_3_out), .out(diodeforward_145_out));
  Button _4 (.out(_4_out));
  DiodeForward diodeforward_153 (.in(_4_out), .out(diodeforward_145_out));
  Button _5 (.out(_5_out));
  DiodeForward diodeforward_154 (.in(_5_out), .out(diodeforward_145_out));
  Button _6 (.out(_6_out));
  DiodeForward diodeforward_155 (.in(_6_out), .out(diodeforward_145_out));
  Button _7 (.out(_7_out));
  DiodeForward diodeforward_156 (.in(_7_out), .out(diodeforward_145_out));
  PullDown pulldown_16 (.out(diodeforward_145_out));
  EEPROM #(.AddrBits(12), .isProgramMemory("true"), .Bits(12)) eeprom_1 (
    .A(ABUS), .CS(~RESET), .WE(~not_3_out), .OE(~not_4_out), .D(DAW[11:0]));
  not not_6 (not_6_out, not_5_out);
  or or_6 (or_6_out, enKEYtoDBUS_1, enDBUStoABUS_0, enKEYtoDBUS_3, enKEYtoDBUS_0);
  DiodeForward diodeforward_157 (.in(_2_out), .out(diodeforward_147_out));
  DiodeForward diodeforward_158 (.in(_3_out), .out(diodeforward_147_out));
  DiodeForward diodeforward_159 (.in(_4_out), .out(diodeforward_148_out));
  DiodeForward diodeforward_160 (.in(_5_out), .out(diodeforward_148_out));
  DiodeForward diodeforward_161 (.in(_6_out), .out(diodeforward_148_out));
  DiodeForward diodeforward_162 (.in(_6_out), .out(diodeforward_147_out));
  DiodeForward diodeforward_163 (.in(_7_out), .out(diodeforward_148_out));
  DiodeForward diodeforward_164 (.in(_7_out), .out(diodeforward_147_out));
  PullDown pulldown_17 (.out(diodeforward_148_out));
  Button R (.out(R_out));
  or or_7 (or_7_out, H_out, BP, STOP);
  Button H (.out(H_out));
  Button S (.out(S_out));
  Button T (.out(T_out));
  and and_4 (and_4_out, T_out, _100Hz);
  Button M (.out(M_out));
  Button P (.out(P_out));
  or or_8 (or_8_out, P_out, PC_rim);
  Button D (.out(D_out));
  or or_9 (or_9_out, D_out, deposit_Rim);
  // Probe on DAW[11:0]
  not not_7 (not_7_out, or_6_out);
  DiodeForward diodeforward_165 (.in(_1_out), .out(diodeforward_146_out));
  DiodeForward diodeforward_166 (.in(_3_out), .out(diodeforward_146_out));
  DiodeForward diodeforward_167 (.in(_5_out), .out(diodeforward_146_out));
  DiodeForward diodeforward_168 (.in(_7_out), .out(diodeforward_146_out));
  PullDown pulldown_18 (.out(diodeforward_147_out));
  PullDown pulldown_19 (.out(diodeforward_146_out));
  OneShot oneshot_2 (.i(or_7_out), .o(oneshot_2_o));
  OneShot oneshot_3 (.i(or_8_out), .o(oneshot_3_o));
  OneShot oneshot_4 (.i(or_9_out), .o(oneshot_4_o));
  Button I (.out(I_out));
  Button W (.out(enKEYtoDBUS_1));
  Button B (.out(enKEYtoDBUS_3));
  Button C (.out(C_out));
  RS_FF_AS rs_ff_as_1 (.S(C_out), .R(1'b0), .nQ(rs_ff_as_1_nq));  // open: Q
  not not_8 (not_8_out, not_6_out);
  _74ls374 _74ls374_1 (
    .Q0(DAW[0]), .Q1(DAW[1]), .Q2(DAW[2]), .Q3(DAW[3]), .Q4(DAW[4]), .Q5(DAW[5]), .Q6(DAW[6]), .Q7(DAW[7]),
    .nOC(not_8_out), .CLK(or_5_out), .D0(_74ls283_1_s1), .D1(_74ls283_1_s2), .D2(_74ls283_1_s3),
    .D3(_74ls283_1_s4), .D4(_74ls283_2_s1), .D5(_74ls283_2_s2), .D6(_74ls283_2_s3), .D7(_74ls283_2_s4));  // open: iv
  _74ls374 _74ls374_2 (
    .Q0(DAW[8]), .Q1(DAW[9]), .Q2(DAW[10]), .Q3(DAW[11]), .nOC(not_8_out), .CLK(or_5_out),
    .D0(_74ls283_3_s1), .D1(_74ls283_3_s2), .D2(_74ls283_3_s3), .D3(_74ls283_3_s4), .D4(1'b0), .D5(1'b0),
    .D6(1'b0), .D7(1'b0));  // open: Q4, Q5, Q6, Q7, iv
  or or_10 (or_10_out, RESET, oneshot_2_o);
  or or_11 (or_11_out, S_out, and_4_out);
  not not_9 (not_9_out, oneshot_3_o);
  not not_10 (not_10_out, oneshot_4_o);
  Delay #(.delayTime(10)) delay_1 (.in(enKEYtoDBUS_1), .out(ckSwitch));
  Delay #(.delayTime(10)) delay_2 (.in(enKEYtoDBUS_3), .out(ckBP));
  or or_12 (RESET, C_out, rs_ff_as_1_nq);
  or or_13 (or_13_out, DAW[0], DAW[1], DAW[2], DAW[3], DAW[4], DAW[5], DAW[6], DAW[7], DAW[8], DAW[9], DAW[10], DAW[11]);
  _74LS541 _74ls541_1 (
    .nOE1(not_7_out), .nOE2(not_7_out), ._0D(_74ls174_1_q6[0]), ._1D(_74ls174_1_q6[1]),
    ._2D(_74ls174_1_q6[2]), ._3D(_74ls174_1_q6[3]), ._4D(_74ls174_1_q6[4]), ._5D(_74ls174_1_q6[5]),
    ._6D(_74ls174_2_q6[0]), ._7D(_74ls174_2_q6[1]), ._0O(DAW[0]), ._1O(DAW[1]), ._2O(DAW[2]), ._3O(DAW[3]),
    ._4O(DAW[4]), ._5O(DAW[5]), ._6O(DAW[6]), ._7O(DAW[7]));
  _74LS541 _74ls541_2 (
    .nOE1(not_7_out), .nOE2(not_7_out), ._0D(_74ls174_2_q6[2]), ._1D(_74ls174_2_q6[3]),
    ._2D(_74ls174_2_q6[4]), ._3D(_74ls174_2_q6[5]), ._4D(1'b0), ._5D(1'b0), ._6D(1'b0), ._7D(1'b0),
    ._0O(DAW[8]), ._1O(DAW[9]), ._2O(DAW[10]), ._3O(DAW[11]));  // open: _4O, _5O, _6O, _7O
  OneShot oneshot_5 (.i(R_out), .o(oneshot_5_o));
  OneShot oneshot_6 (.i(or_11_out), .o(oneshot_6_o));
  or or_14 (or_14_out, iDone, RESET);
  _74LS74 _74ls74_2 (
    ._1nSD(not_9_out), ._1D(1'b0), ._1CP(1'b0), ._1nRD(_74ls139_1_n1y3), ._2nSD(not_10_out), ._2D(1'b0),
    ._2CP(1'b0), ._2nRD(_74ls139_1_n2y3), ._1nQ(_74ls74_2__1nq), ._2nQ(_74ls74_2__2nq));  // open: _1Q, _2Q
  // Probe on RESET
  not not_11 (fDBUSisZero, or_13_out);
  not not_12 (nRESET, RESET);
  _74LS174 _74ls174_1 (
    .D1(diodeforward_146_out), .D2(diodeforward_147_out), .D3(diodeforward_148_out), .D4(_74ls174_1_q6[0]),
    .D5(_74ls174_1_q6[1]), .D6(_74ls174_1_q6[2]), .CLK(diodeforward_145_out), .nCL(nRESET),
    .Q1(_74ls174_1_q6[0]), .Q2(_74ls174_1_q6[1]), .Q3(_74ls174_1_q6[2]), .Q4(_74ls174_1_q6[3]),
    .Q5(_74ls174_1_q6[4]), .Q6(_74ls174_1_q6[5]));
  _74LS74 _74ls74_3 (
    ._1nSD(not_13_out), ._1D(1'b0), ._1CP(1'b0), ._1nRD(not_14_out), ._2nSD(not_15_out), ._2D(1'b0),
    ._2CP(1'b0), ._2nRD(not_16_out), ._1Q(_74ls74_3__1q), ._1nQ(_74ls74_3__1nq), ._2Q(_74ls74_3__2q));  // open: _2nQ
  not not_13 (not_13_out, oneshot_5_o);
  not not_14 (not_14_out, or_10_out);
  not not_15 (not_15_out, oneshot_6_o);
  not not_16 (not_16_out, or_14_out);
  _74LS393 _74ls393_2 (
    ._1A(_100Hz), ._1CL(_74ls74_2__1nq), ._2A(_100Hz), ._2CL(_74ls74_2__2nq), ._1QB(_74ls393_2__1qb),
    ._1QC(_74ls393_2__1qc), ._2QA(_74ls393_2__2qa), ._2QB(_74ls393_2__2qb));  // open: _1QA, _1QD, _2QC, _2QD
  _74LS85 _74ls85_1 (
    .P_lt_Q_i(1'b0), .P_eq_Q_i(1'b1), .P_gt_Q_i(1'b0), .P_0(BPaddress[0]), .P_1(BPaddress[1]),
    .P_2(BPaddress[2]), .P_3(BPaddress[3]), .Q_0(IRA[0]), .Q_1(IRA[1]), .Q_2(IRA[2]), .Q_3(IRA[3]),
    .P_lt_Q(_74ls85_1_p_lt_q[0]), .P_eq_Q(_74ls85_1_p_lt_q[1]), .P_gt_Q(_74ls85_1_p_lt_q[2]));
  _74LS85 _74ls85_2 (
    .P_lt_Q_i(_74ls85_1_p_lt_q[0]), .P_eq_Q_i(_74ls85_1_p_lt_q[1]), .P_gt_Q_i(_74ls85_1_p_lt_q[2]),
    .P_0(BPaddress[4]), .P_1(BPaddress[5]), .P_2(BPaddress[6]), .P_3(BPaddress[7]), .Q_0(IRA[4]),
    .Q_1(IRA[5]), .Q_2(IRA[6]), .Q_3(IRA[7]), .P_lt_Q(_74ls85_2_p_lt_q[0]), .P_eq_Q(_74ls85_2_p_lt_q[1]),
    .P_gt_Q(_74ls85_2_p_lt_q[2]));
  _74LS85 _74ls85_3 (
    .P_lt_Q_i(_74ls85_2_p_lt_q[0]), .P_eq_Q_i(_74ls85_2_p_lt_q[1]), .P_gt_Q_i(_74ls85_2_p_lt_q[2]),
    .P_0(_74ls273_2_q4), .P_1(_74ls273_2_q5), .P_2(_74ls273_2_q6), .P_3(_74ls273_2_q7), .Q_0(IRA[8]),
    .Q_1(IRA[9]), .Q_2(IRA[10]), .Q_3(IRA[11]), .P_eq_Q(_74ls85_3_p_eq_q));  // open: P_lt_Q, P_gt_Q
  OneShot oneshot_7 (.i(_74ls74_3__1q), .o(oneshot_7_o));
  or or_15 (or_15_out, _74ls74_3__1nq, _74ls74_3__2q);
  PullDown pulldown_20 (.out(enDBUStoABUS_rim));
  PullDown pulldown_21 (.out(ckDBUStoABUS_rim));
  and and_5 (and_5_out, or_15_out, iDone);
  _74LS139 _74ls139_1 (
    .n1G(_74ls74_2__1nq), ._1A(_74ls393_2__1qb), ._1B(_74ls393_2__1qc), .n2G(_74ls74_2__2nq),
    ._2A(_74ls393_2__2qa), ._2B(_74ls393_2__2qb), .n1Y0(_74ls139_1_n1y0), .n1Y1(_74ls139_1_n1y1),
    .n1Y2(_74ls139_1_n1y2), .n1Y3(_74ls139_1_n1y3), .n2Y0(_74ls139_1_n2y0), .n2Y1(_74ls139_1_n2y1),
    .n2Y2(_74ls139_1_n2y2), .n2Y3(_74ls139_1_n2y3));
  or or_16 (or_16_out, enDBUStoABUS_andtad, ckDBUStoABUS_jmp, ckDBUStoABUS_jms, enDBUStoABUS_rim, ckDBUStoABUS_isz, enDBUStoABUS_dca, enDBUStoABUS_0);
  or or_17 (or_17_out, ckDBUStoABUS_andtad, ckDBUStoABUS_jmp, ckDBUStoABUS_jms, ckDBUStoABUS_rim, ckDBUStoABUS_isz, ckDBUStoABUS_dca, ckDBUStoABUS_0);
  and and_6 (BP, _74ls85_3_p_eq_q, in_3, ckIR);
  _74LS174 _74ls174_2 (
    .D1(_74ls174_1_q6[3]), .D2(_74ls174_1_q6[4]), .D3(_74ls174_1_q6[5]), .D4(_74ls174_2_q6[0]),
    .D5(_74ls174_2_q6[1]), .D6(_74ls174_2_q6[2]), .CLK(diodeforward_145_out), .nCL(nRESET),
    .Q1(_74ls174_2_q6[0]), .Q2(_74ls174_2_q6[1]), .Q3(_74ls174_2_q6[2]), .Q4(_74ls174_2_q6[3]),
    .Q5(_74ls174_2_q6[4]), .Q6(_74ls174_2_q6[5]));
  or or_18 (or_18_out, oneshot_6_o, oneshot_7_o);
  OneShot oneshot_8 (.i(and_5_out), .o(oneshot_8_o));
  or or_19 (or_19_out, oneshot_8_o, RESET);
  not not_17 (enDBUStoABUS_0, _74ls139_1_n1y0);
  not not_18 (not_18_out, _74ls139_1_n1y1);
  // Not not_19 has open pins: in=_74ls139_1_n1y2, out=open
  not not_20 (enKEYtoDBUS_0, _74ls139_1_n2y0);
  not not_21 (not_21_out, _74ls139_1_n2y1);
  // Not not_22 has open pins: in=_74ls139_1_n2y2, out=open
  not not_23 (not_23_out, or_18_out);
  not not_24 (not_24_out, or_19_out);
  or or_20 (or_20_out, enINSTRtoABUS_jmp, enINSTRtoABUS_andtad, enINSTRtoABUS_dca, enINSTRtoABUS_ai, enINSTRtoABUS_dca, enINSTRtoABUS_isz, enINSTRtoABUS_jms);
  not not_25 (not_25_out, or_16_out);
  _74ls374 _74ls374_3 (
    .Q0(ABUS[0]), .Q1(ABUS[1]), .Q2(ABUS[2]), .Q3(ABUS[3]), .Q4(ABUS[4]), .Q5(ABUS[5]), .Q6(ABUS[6]),
    .Q7(ABUS[7]), .nOC(not_25_out), .CLK(or_17_out), .D0(DAW[0]), .D1(DAW[1]), .D2(DAW[2]), .D3(DAW[3]),
    .D4(DAW[4]), .D5(DAW[5]), .D6(DAW[6]), .D7(DAW[7]));  // open: iv
  _74ls374 _74ls374_4 (
    .Q0(ABUS[8]), .Q1(ABUS[9]), .Q2(ABUS[10]), .Q3(ABUS[11]), .nOC(not_25_out), .CLK(or_17_out), .D0(DAW[8]),
    .D1(DAW[9]), .D2(DAW[10]), .D3(DAW[11]), .D4(1'b0), .D5(1'b0), .D6(1'b0), .D7(1'b0));  // open: Q4, Q5, Q6, Q7, iv
  OneShot oneshot_9 (.i(enKEYtoDBUS_0), .o(weRAM_rim));
  // Probe on DAW[11:0]
  _74LS74 _74ls74_4 (
    ._1nSD(not_23_out), ._1D(1'b0), ._1CP(1'b0), ._1nRD(not_24_out), ._2nSD(1'b1), ._2D(_74ls74_4__1q),
    ._2CP(MAX), ._2nRD(1'b1), ._1Q(_74ls74_4__1q), ._2Q(_74ls74_4__2q));  // open: _1nQ, _2nQ
  not not_26 (not_26_out, enALUor_mop2);
  _74LS247 _74ls247_1 (
    .A(_74ls153_3__1y), .B(_74ls153_3__2y), .C(_74ls153_4__1y), .D(1'b0), .nRBI(1'b1), .nLT(1'b1),
    .nBI_nRBO(1'b1), .na(_74ls247_1_na), .nb(_74ls247_1_nb), .nc(_74ls247_1_nc), .nd(_74ls247_1_nd),
    .ne(_74ls247_1_ne), .nf(_74ls247_1_nf), .ng(_74ls247_1_ng));
  _74LS153 _74ls153_3 (
    ._1G(1'b0), ._1C0(_74ls174_1_q6[0]), ._1C1(_74ls174_1_q6[3]), ._1C2(_74ls174_2_q6[0]),
    ._1C3(_74ls174_2_q6[3]), ._2G(1'b0), ._2C0(_74ls174_1_q6[1]), ._2C1(_74ls174_1_q6[4]),
    ._2C2(_74ls174_2_q6[1]), ._2C3(_74ls174_2_q6[4]), .A(_74ls161_1_qa), .B(_74ls161_1_qb),
    ._1Y(_74ls153_3__1y), ._2Y(_74ls153_3__2y));
  _74LS153 _74ls153_4 (
    ._1G(1'b0), ._1C0(_74ls174_1_q6[2]), ._1C1(_74ls174_1_q6[5]), ._1C2(_74ls174_2_q6[2]),
    ._1C3(_74ls174_2_q6[5]), ._2G(1'b0), ._2C0(1'b0), ._2C1(1'b0), ._2C2(1'b0), ._2C3(1'b0),
    .A(_74ls161_1_qa), .B(_74ls161_1_qb), ._1Y(_74ls153_4__1y));  // open: _2Y
  or or_21 (or_21_out, not_21_out, I_out);
  or or_22 (ckIR, ckIR_0, ckIR_irq, ckIR_LoadIR);
  and and_7 (and_7_out, PC[7], isCurrPage);
  and and_8 (and_8_out, PC[8], isCurrPage);
  and and_9 (and_9_out, PC[9], isCurrPage);
  and and_10 (and_10_out, PC[10], isCurrPage);
  and and_11 (and_11_out, PC[11], isCurrPage);
  _74LS273 _74ls273_3 (
    .CP(ckSwitch), .nMR(nRESET), .D0(DAW[0]), .D1(DAW[1]), .D2(DAW[2]), .D3(DAW[3]), .D4(DAW[4]),
    .D5(DAW[5]), .D6(DAW[6]), .D7(DAW[7]), .Q0(switch[0]), .Q1(switch[1]), .Q2(switch[2]), .Q3(switch[3]),
    .Q4(switch[4]), .Q5(switch[5]), .Q6(switch[6]), .Q7(switch[7]));
  _74LS273 _74ls273_4 (
    .CP(ckSwitch), .nMR(nRESET), .D0(DAW[8]), .D1(DAW[9]), .D2(DAW[10]), .D3(DAW[11]), .D4(1'b0), .D5(1'b0),
    .D6(1'b0), .D7(1'b0), .Q0(switch[8]), .Q1(switch[9]), .Q2(switch[10]), .Q3(switch[11]));  // open: Q4, Q5, Q6, Q7
  and and_12 (and_12_out, _74ls74_4__2q, MAX);
  OneShot oneshot_10 (.i(or_21_out), .o(oneshot_10_o));
  not not_27 (not_27_out, or_20_out);
  or or_23 (CLK_t, and_12_out, M_out);
  or or_24 (enPCtoABUS_0, not_18_out, oneshot_10_o);
  _74LS273 _74ls273_5 (
    .CP(ckIR), .nMR(nRESET), .D0(PC[0]), .D1(PC[1]), .D2(PC[2]), .D3(PC[3]), .D4(PC[4]), .D5(PC[5]),
    .D6(PC[6]), .D7(PC[7]), .Q0(IRA[0]), .Q1(IRA[1]), .Q2(IRA[2]), .Q3(IRA[3]), .Q4(IRA[4]), .Q5(IRA[5]),
    .Q6(IRA[6]), .Q7(IRA[7]));
  _74LS273 _74ls273_6 (
    .CP(ckIR), .nMR(nRESET), .D0(PC[8]), .D1(PC[9]), .D2(PC[10]), .D3(PC[11]), .D4(1'b0), .D5(1'b0),
    .D6(1'b0), .D7(1'b0), .Q0(IRA[8]), .Q1(IRA[9]), .Q2(IRA[10]), .Q3(IRA[11]));  // open: Q4, Q5, Q6, Q7
  _74LS273 _74ls273_7 (
    .CP(ckIR), .nMR(nRESET), .D0(DAW[0]), .D1(DAW[1]), .D2(DAW[2]), .D3(DAW[3]), .D4(DAW[4]), .D5(DAW[5]),
    .D6(DAW[6]), .D7(DAW[7]), .Q0(IR[0]), .Q1(IR[1]), .Q2(IR[2]), .Q3(IR[3]), .Q4(IR[4]), .Q5(IR[5]),
    .Q6(IR[6]), .Q7(IR[7]));
  _74LS273 _74ls273_8 (
    .CP(ckIR), .nMR(nRESET), .D0(DAW[8]), .D1(DAW[9]), .D2(DAW[10]), .D3(DAW[11]), .D4(1'b0), .D5(1'b0),
    .D6(1'b0), .D7(1'b0), .Q0(IR[8]), .Q1(IR[9]), .Q2(IR[10]), .Q3(IR[11]));  // open: Q4, Q5, Q6, Q7
  _74LS244 _74ls244_1 (
    ._1A1(IR[0]), ._1A2(IR[1]), ._1A3(IR[2]), ._1A4(IR[3]), ._1nG(not_27_out), ._2A1(IR[4]), ._2A2(IR[5]),
    ._2A3(IR[6]), ._2A4(and_7_out), ._2nG(not_27_out), ._1Y1(ABUS[0]), ._1Y2(ABUS[1]), ._1Y3(ABUS[2]),
    ._1Y4(ABUS[3]), ._2Y1(ABUS[4]), ._2Y2(ABUS[5]), ._2Y3(ABUS[6]), ._2Y4(ABUS[7]));
  _74LS244 _74ls244_2 (
    ._1A1(and_8_out), ._1A2(and_9_out), ._1A3(and_10_out), ._1A4(and_11_out), ._1nG(not_27_out), ._2A1(1'b1),
    ._2A2(1'b1), ._2A3(1'b1), ._2A4(1'b1), ._2nG(1'b1), ._1Y1(ABUS[8]), ._1Y2(ABUS[9]), ._1Y3(ABUS[10]),
    ._1Y4(ABUS[11]));  // open: _2Y1, _2Y2, _2Y3, _2Y4
  Seven_Seg #(.commonCathode("true"), .commonConnectionType("anode"), .persistTime(10000)) seven_seg_1 (
    .a(_74ls247_1_na), .b(_74ls247_1_nb), .c(_74ls247_1_nc), .d(_74ls247_1_nd), .e(_74ls247_1_ne),
    .f(_74ls247_1_nf), .g(_74ls247_1_ng), .dp(1'b1), .common(_74ls238_4_y3));
  // Probe on CLK_t
  Seven_Seg #(.commonCathode("true"), .commonConnectionType("anode"), .persistTime(10000)) seven_seg_2 (
    .a(_74ls247_1_na), .b(_74ls247_1_nb), .c(_74ls247_1_nc), .d(_74ls247_1_nd), .e(_74ls247_1_ne),
    .f(_74ls247_1_nf), .g(_74ls247_1_ng), .dp(1'b1), .common(_74ls238_4_y2));
  _74LS238 _74ls238_4 (
    .A(_74ls161_1_qa), .B(_74ls161_1_qb), .C(1'b0), .G(1'b1), .nGB(1'b0), .nGA(1'b0), .Y0(_74ls238_4_y0),
    .Y1(_74ls238_4_y1), .Y2(_74ls238_4_y2), .Y3(_74ls238_4_y3));  // open: Y4, Y5, Y6, Y7
  _74LS161 _74ls161_1 (
    .CLK(clk), .A(1'b1), .B(1'b1), .C(1'b1), .D(1'b1), .nLD(1'b1), .nCLR(1'b1), .ENT(1'b1), .ENP(1'b1),
    .QA(_74ls161_1_qa), .QB(_74ls161_1_qb));  // open: QC, QD, RCO
  Delay #(.delayTime(10)) delay_3 (.in(enDBUStoABUS_0), .out(ckDBUStoABUS_0));
  Delay #(.delayTime(10)) delay_4 (.in(delay_5_out), .out(ckSetPC_0));
  Delay #(.delayTime(10)) delay_5 (.in(enDBUStoABUS_0), .out(delay_5_out));
  Delay #(.delayTime(10)) delay_6 (.in(enPCtoABUS_0), .out(ckIR_0));
  Delay #(.delayTime(10)) delay_7 (.in(delay_8_out), .out(delay_7_out));
  Delay #(.delayTime(10)) delay_8 (.in(enPCtoABUS_0), .out(delay_8_out));
  Seven_Seg #(.commonCathode("true"), .commonConnectionType("anode"), .persistTime(10000)) seven_seg_3 (
    .a(_74ls247_1_na), .b(_74ls247_1_nb), .c(_74ls247_1_nc), .d(_74ls247_1_nd), .e(_74ls247_1_ne),
    .f(_74ls247_1_nf), .g(_74ls247_1_ng), .dp(1'b1), .common(_74ls238_4_y1));
  and and_13 (ckIncPC_inc, delay_7_out, or_21_out);
  _74LS541 _74ls541_3 (
    .nOE1(not_26_out), .nOE2(not_26_out), ._0D(switch[0]), ._1D(switch[1]), ._2D(switch[2]), ._3D(switch[3]),
    ._4D(switch[4]), ._5D(switch[5]), ._6D(switch[6]), ._7D(switch[7]), ._0O(OBUS[0]), ._1O(OBUS[1]),
    ._2O(OBUS[2]), ._3O(OBUS[3]), ._4O(OBUS[4]), ._5O(OBUS[5]), ._6O(OBUS[6]), ._7O(OBUS[7]));
  _74LS541 _74ls541_4 (
    .nOE1(not_26_out), .nOE2(not_26_out), ._0D(switch[8]), ._1D(switch[9]), ._2D(switch[10]),
    ._3D(switch[11]), ._4D(1'b0), ._5D(1'b0), ._6D(1'b0), ._7D(1'b0), ._0O(OBUS[8]), ._1O(OBUS[9]),
    ._2O(OBUS[10]), ._3O(OBUS[11]));  // open: _4O, _5O, _6O, _7O
  Seven_Seg #(.commonCathode("true"), .commonConnectionType("anode"), .persistTime(10000)) seven_seg_4 (
    .a(_74ls247_1_na), .b(_74ls247_1_nb), .c(_74ls247_1_nc), .d(_74ls247_1_nd), .e(_74ls247_1_ne),
    .f(_74ls247_1_nf), .g(_74ls247_1_ng), .dp(1'b1), .common(_74ls238_4_y0));
  // Probe on OBUS
  SixteenSeg sixteenseg_1 (.led(CharRom3x_d[15:0]), .dp(CharRom3x_d[50]));
  SixteenSeg sixteenseg_2 (.led(CharRom3x_d[31:16]), .dp(CharRom3x_d[50]));
  ROM #(.AddrBits(12), .Bits(51)) CharRom3x (
    .A(IR), .sel(1'b1), .D({CharRom3x_d[50], fIndirect, isCurrPage, CharRom3x_d[47:0]}));
  LED led_1 (.in(L_GEN[10]));
  LED led_2 (.in(AND));
  LED led_3 (.in(fGIE));
  LED led_4 (.in(L_IRQ[5]));
  LED led_5 (.in(CLA_1));
  LED led_6 (.in(L_OPR1[10]));
  LED led_7 (.in(L_OPR2[8]));
  LED led_8 (.in(CLA_2));
  LED led_9 (.in(L_OPR3[12]));
  LED led_10 (.in(CLA_3));
  LED led_11 (.in(L_CPU[7]));
  LED led_12 (.in(ION_6001));
  LED led_13 (.in(KCF_6030));
  LED led_14 (.in(KSF_6031));
  LED led_15 (.in(L_PRN[4]));
  LED led_16 (.in(L_PRN[5]));
  SixteenSeg sixteenseg_3 (.led(CharRom3x_d[47:32]), .dp(CharRom3x_d[50]));
  LED led_17 (.in(ISZ));
  LED led_18 (.in(fIrqDly));
  LED led_19 (.in(CLL));
  LED led_20 (.in(L_OPR2[7]));
  LED led_21 (.in(L_OPR3[10]));
  LED led_22 (.in(IOF_6002));
  LED led_23 (.in(KCC_6032));
  LED led_24 (.in(L_PRN[3]));
  Seven_Seg_Hex seven_seg_hex_1 (.d({3'b000, IR[6]}), .dp(1'b0));
  LED led_25 (.in(DCA));
  LED led_26 (.in(enIRQ));
  LED led_27 (.in(CMA));
  LED led_28 (.in(L_OPR2[6]));
  LED led_29 (.in(L_OPR3[9]));
  LED led_30 (.in(L_CPU[4]));
  LED led_31 (.in(KRS_6034));
  LED led_32 (.in(L_PRN[2]));
  Seven_Seg_Hex seven_seg_hex_2 (.d({1'b0, IR[5:3]}), .dp(1'b0));
  LED CURRENT_PAGE (.in(isCurrPage));
  LED u_INDIRECT (.in(fIndirect));
  not not_28 (not_28_out, IR[4]);
  not not_29 (not_29_out, IR[5]);
  not not_30 (not_30_out, IR[6]);
  not not_31 (not_31_out, isCurrPage);
  LED led_33 (.in(JMS));
  LED led_34 (.in(JMP));
  LED led_35 (.in(L_IRQ[2]));
  LED led_36 (.in(fKBD));
  LED led_37 (.in(CML));
  LED led_38 (.in(IAC));
  LED led_39 (.in(L_OPR2[4]));
  LED led_40 (.in(L_OPR2[5]));
  LED led_41 (.in(L_OPR3[8]));
  LED led_42 (.in(L_OPR3[7]));
  LED led_43 (.in(GTF_6004));
  LED led_44 (.in(L_CPU[2]));
  LED led_45 (.in(KIE_6035));
  LED led_46 (.in(KRB_6036));
  LED led_47 (.in(L_PRN[1]));
  LED led_48 (.in(L_PRN[0]));
  Seven_Seg_Hex seven_seg_hex_3 (.d({1'b0, IR[2:0]}), .dp(1'b0));
  and and_14 (fAutoinc, fIndirect, IR[3], not_28_out, not_29_out, not_30_out, not_31_out);
  LED led_49 (.in(IOT));
  LED led_50 (.in(fPRN));
  LED led_51 (.in(L_OPR1[4]));
  LED led_52 (.in(L_OPR2[3]));
  LED led_53 (.in(L_OPR3[6]));
  LED led_54 (.in(L_CPU[1]));
  LED led_55 (.in(L_GEN[4]));
  LED led_56 (.in(L_OPR1[3]));
  LED led_57 (.in(L_OPR2[2]));
  LED led_58 (.in(L_OPR3[5]));
  LED led_59 (.in(CAF_6007));
  LED led_60 (.in(L_GEN[3]));
  LED led_61 (.in(fIndirect));
  LED led_62 (.in(L_OPR1[2]));
  LED led_63 (.in(L_OPR1[1]));
  LED led_64 (.in(L_OPR2[1]));
  LED led_65 (.in(HLT));
  LED led_66 (.in(L_OPR3[4]));
  LED led_67 (.in(L_OPR3[3]));
  or or_25 (or_25_out, ckIncPC_LoadIR, ckIncPC_jms1, ckIncPC_irq1, 1'b0, ckIncPC_inc, not_36_out);
  or or_26 (or_26_out, ckSetPC_0, ckSetPC_jmp, ckSetPC_jms);
  or or_27 (or_27_out, enPCtoABUS_0, enPCtoABUS_LoadIR, enPCtoABUS_irq, enPCtoABUS_mop2, enKEYtoDBUS_0);
  or or_28 (or_28_out, clrPC_irq, RESET);
  or or_29 (or_29_out, ckIncPC_jms1, enPCtoDBUS_irq);
  RAMSPY ramspy_1 (.Trig({12{1'b0}}), .DAW({DAW[24], ABUS, DAW[11:0]}), .O(ramspy_1_o));
  RAMSPY ramspy_2 (.Trig(12'h51), .DAW({DAW[24], ABUS, DAW[11:0]}), .O(ramspy_2_o));
  LED led_68 (.in(fAutoinc));
  LED led_69 (.in(BSW));
  LED led_70 (.in(L_OPR3[2]));
  not not_32 (not_32_out, or_26_out);
  not not_33 (not_33_out, or_27_out);
  not not_34 (not_34_out, or_28_out);
  not not_35 (not_35_out, or_29_out);
  // Probe on iDone
  LED led_71 (.in(isCurrPage));
  LED led_72 (.in(L_OPR3[1]));
  OneShot oneshot_11 (.i(_1Hz), .o(oneshot_11_o));
  not not_36 (not_36_out, not_32_out);
  // Probe on ramspy_1_o
  // Probe on ramspy_2_o
  LED led_73 (.in(L_OPR3[0]));
  T_FF t_ff_1 (.T(1'b1), .C(oneshot_11_o), .Q(t_ff_1_q));  // open: nQ
  Seven_Seg_Hex seven_seg_hex_4 (.d({1'b0, IR[11:9]}), .dp(1'b0));
  Seven_Seg_Hex seven_seg_hex_5 (.d({1'b0, ACC11, ACCC[10:9]}), .dp(1'b0));
  LED led_74 (.in(LINK));
  Seven_Seg_Hex seven_seg_hex_6 (.d({1'b0, MQ[11:9]}), .dp(1'b0));
  Counter #(.Bits(20)) counter_1 (.en(1'b1), .C(iDone), .clr(t_ff_1_q), .out(counter_1_out));  // open: ovf
  Seven_Seg_Hex seven_seg_hex_7 (.d({1'b0, IRA[11:9]}), .dp(1'b0));
  Seven_Seg_Hex seven_seg_hex_8 (.d({1'b0, IR[8:6]}), .dp(1'b0));
  Seven_Seg_Hex seven_seg_hex_9 (.d({1'b0, ACCC[8:6]}), .dp(1'b0));
  Seven_Seg_Hex seven_seg_hex_10 (.d({1'b0, MQ[8:6]}), .dp(1'b0));
  D_FF #(.Bits(20)) d_ff_1 (.D(counter_1_out), .C(t_ff_1_q), .Q(d_ff_1_q));  // open: nQ
  _74LS161 _74ls161_2 (
    .CLK(or_25_out), .A(ABUS[0]), .B(ABUS[1]), .C(ABUS[2]), .D(ABUS[3]), .nLD(not_32_out), .nCLR(not_34_out),
    .ENT(1'b1), .ENP(1'b1), .QA(PC[0]), .QB(PC[1]), .QC(PC[2]), .QD(PC[3]), .RCO(_74ls161_2_rco));
  _74LS161 _74ls161_3 (
    .CLK(or_25_out), .A(ABUS[4]), .B(ABUS[5]), .C(ABUS[6]), .D(ABUS[7]), .nLD(not_32_out), .nCLR(not_34_out),
    .ENT(_74ls161_2_rco), .ENP(_74ls161_2_rco), .QA(PC[4]), .QB(PC[5]), .QC(PC[6]), .QD(PC[7]),
    .RCO(_74ls161_3_rco));
  _74LS161 _74ls161_4 (
    .CLK(or_25_out), .A(ABUS[8]), .B(ABUS[9]), .C(ABUS[10]), .D(ABUS[11]), .nLD(not_32_out),
    .nCLR(not_34_out), .ENT(_74ls161_3_rco), .ENP(_74ls161_3_rco), .QA(PC[8]), .QB(PC[9]), .QC(PC[10]),
    .QD(PC[11]));  // open: RCO
  Seven_Seg_Hex seven_seg_hex_11 (.d({1'b0, IRA[8:6]}), .dp(1'b0));
  Seven_Seg_Hex seven_seg_hex_12 (.d({1'b0, IR[5:3]}), .dp(1'b0));
  Seven_Seg_Hex seven_seg_hex_13 (.d({1'b0, ACCC[5:3]}), .dp(1'b0));
  Seven_Seg_Hex seven_seg_hex_14 (.d({1'b0, MQ[5:3]}), .dp(1'b0));
  // Probe on d_ff_1_q
  Seven_Seg_Hex seven_seg_hex_15 (.d({1'b0, IRA[5:3]}), .dp(1'b0));
  Seven_Seg_Hex seven_seg_hex_16 (.d({1'b0, IR[2:0]}), .dp(1'b0));
  Seven_Seg_Hex seven_seg_hex_17 (.d({1'b0, ACCC[2:0]}), .dp(1'b0));
  Seven_Seg_Hex seven_seg_hex_18 (.d({1'b0, MQ[2:0]}), .dp(1'b0));
  Seven_Seg_Hex seven_seg_hex_19 (.d({1'b0, IRA[2:0]}), .dp(1'b0));
  _74LS244 _74ls244_3 (
    ._1A1(PC[0]), ._1A2(PC[1]), ._1A3(PC[2]), ._1A4(PC[3]), ._1nG(not_33_out), ._2A1(PC[4]), ._2A2(PC[5]),
    ._2A3(PC[6]), ._2A4(PC[7]), ._2nG(not_33_out), ._1Y1(ABUS[0]), ._1Y2(ABUS[1]), ._1Y3(ABUS[2]),
    ._1Y4(ABUS[3]), ._2Y1(ABUS[4]), ._2Y2(ABUS[5]), ._2Y3(ABUS[6]), ._2Y4(ABUS[7]));
  _74LS244 _74ls244_4 (
    ._1A1(PC[8]), ._1A2(PC[9]), ._1A3(PC[10]), ._1A4(PC[11]), ._1nG(not_33_out), ._2A1(1'b1), ._2A2(1'b1),
    ._2A3(1'b1), ._2A4(1'b1), ._2nG(1'b1), ._1Y1(ABUS[8]), ._1Y2(ABUS[9]), ._1Y3(ABUS[10]), ._1Y4(ABUS[11]));  // open: _2Y1, _2Y2, _2Y3, _2Y4
  _74LS244 _74ls244_5 (
    ._1A1(PC[0]), ._1A2(PC[1]), ._1A3(PC[2]), ._1A4(PC[3]), ._1nG(not_35_out), ._2A1(PC[4]), ._2A2(PC[5]),
    ._2A3(PC[6]), ._2A4(PC[7]), ._2nG(not_35_out), ._1Y1(DAW[0]), ._1Y2(DAW[1]), ._1Y3(DAW[2]),
    ._1Y4(DAW[3]), ._2Y1(DAW[4]), ._2Y2(DAW[5]), ._2Y3(DAW[6]), ._2Y4(DAW[7]));
  _74LS244 _74ls244_6 (
    ._1A1(PC[8]), ._1A2(PC[9]), ._1A3(PC[10]), ._1A4(PC[11]), ._1nG(not_35_out), ._2A1(1'b1), ._2A2(1'b1),
    ._2A3(1'b1), ._2A4(1'b1), ._2nG(1'b1), ._1Y1(DAW[8]), ._1Y2(DAW[9]), ._1Y3(DAW[10]), ._1Y4(DAW[11]));  // open: _2Y1, _2Y2, _2Y3, _2Y4
  Seven_Seg_Hex seven_seg_hex_20 (.d({1'b0, ABUS[11:9]}), .dp(1'b0));
  Seven_Seg_Hex seven_seg_hex_21 (.d({1'b0, DAW[11:9]}), .dp(1'b0));
  Seven_Seg_Hex seven_seg_hex_22 (.d({1'b0, OBUS[11:9]}), .dp(1'b0));
  Seven_Seg_Hex seven_seg_hex_23 (.d({1'b0, switch[11:9]}), .dp(1'b0));
  Seven_Seg_Hex seven_seg_hex_24 (.d({1'b0, BPaddress[11:9]}), .dp(1'b0));
  Seven_Seg_Hex seven_seg_hex_25 (.d({1'b0, ABUS[8:6]}), .dp(1'b0));
  Seven_Seg_Hex seven_seg_hex_26 (.d({1'b0, DAW[8:6]}), .dp(1'b0));
  Seven_Seg_Hex seven_seg_hex_27 (.d({1'b0, OBUS[8:6]}), .dp(1'b0));
  Seven_Seg_Hex seven_seg_hex_28 (.d({1'b0, switch[8:6]}), .dp(1'b0));
  Seven_Seg_Hex seven_seg_hex_29 (.d({1'b0, BPaddress[8:6]}), .dp(1'b0));
  Seven_Seg_Hex seven_seg_hex_30 (.d({1'b0, ABUS[5:3]}), .dp(1'b0));
  Seven_Seg_Hex seven_seg_hex_31 (.d({1'b0, DAW[5:3]}), .dp(1'b0));
  Seven_Seg_Hex seven_seg_hex_32 (.d({1'b0, OBUS[5:3]}), .dp(1'b0));
  Seven_Seg_Hex seven_seg_hex_33 (.d({1'b0, switch[5:3]}), .dp(1'b0));
  Seven_Seg_Hex seven_seg_hex_34 (.d({1'b0, BPaddress[5:3]}), .dp(1'b0));
  Seven_Seg_Hex seven_seg_hex_35 (.d({1'b0, ABUS[2:0]}), .dp(1'b0));
  Seven_Seg_Hex seven_seg_hex_36 (.d({1'b0, DAW[2:0]}), .dp(1'b0));
  Seven_Seg_Hex seven_seg_hex_37 (.d({1'b0, OBUS[2:0]}), .dp(1'b0));
  Seven_Seg_Hex seven_seg_hex_38 (.d({1'b0, switch[2:0]}), .dp(1'b0));
  Seven_Seg_Hex seven_seg_hex_39 (.d({1'b0, BPaddress[2:0]}), .dp(1'b0));
  PullDown pulldown_22 (.out(L_OPR3[0]));
  PullDown pulldown_23 (.out(L_OPR3[1]));
  PullDown pulldown_24 (.out(L_OPR3[2]));
  PullDown pulldown_25 (.out(L_OPR3[3]));
  PullDown pulldown_26 (.out(L_OPR3[4]));
  PullDown pulldown_27 (.out(L_OPR3[5]));
  PullDown pulldown_28 (.out(L_OPR3[6]));
  PullDown pulldown_29 (.out(L_GEN[3]));
  PullDown pulldown_30 (.out(L_IRQ[2]));
  PullDown pulldown_31 (.out(L_OPR3[12]));
  PullDown pulldown_32 (.out(L_OPR1[10]));
  PullDown pulldown_33 (.out(L_IRQ[5]));
  _74LS238 _74ls238_5 (
    .A(IR[9]), .B(IR[10]), .C(IR[11]), .G(1'b1), .nGB(RESET), .nGA(inhibitIR), .Y0(AND), .Y1(L_GEN[10]),
    .Y2(ISZ), .Y3(DCA), .Y4(JMS), .Y5(JMP), .Y6(IOT), .Y7(L_GEN[4]));
  not not_37 (not_37_out, IR[0]);
  not not_38 (not_38_out, IR[8]);
  _74LS238 _74ls238_6 (
    .A(IR[3]), .B(IR[4]), .C(IR[5]), .G(IOT), .nGB(1'b0), .nGA(1'b0), .Y0(IOT_CPU), .Y1(IOT_HISPEEDREADER),
    .Y2(IOT_HISPEEDPUNCH), .Y3(IOT_TTYREADER), .Y4(IOT_TTYPUNCH));  // open: Y5, Y6, Y7
  _74LS238 _74ls238_7 (
    .A(IR[0]), .B(IR[1]), .C(IR[2]), .G(IOT_CPU), .nGB(1'b0), .nGA(1'b0), .Y0(L_CPU[7]), .Y1(ION_6001),
    .Y2(IOF_6002), .Y3(L_CPU[4]), .Y4(GTF_6004), .Y5(L_CPU[2]), .Y6(L_CPU[1]), .Y7(CAF_6007));
  _74LS238 _74ls238_8 (
    .A(IR[0]), .B(IR[1]), .C(IR[2]), .G(IOT_TTYREADER), .nGB(1'b0), .nGA(1'b0), .Y0(KCF_6030), .Y1(KSF_6031),
    .Y2(KCC_6032), .Y4(KRS_6034), .Y5(KIE_6035), .Y6(KRB_6036));  // open: Y3, Y7
  _74LS238 _74ls238_9 (
    .A(IR[0]), .B(IR[1]), .C(IR[2]), .G(IOT_TTYPUNCH), .nGB(1'b0), .nGA(1'b0), .Y0(L_PRN[5]), .Y1(L_PRN[4]),
    .Y2(L_PRN[3]), .Y4(L_PRN[2]), .Y5(L_PRN[1]), .Y6(L_PRN[0]));  // open: Y3, Y7
  and and_15 (MOP3, IR[0], IR[8], L_GEN[4]);
  and and_16 (MOP2, not_37_out, IR[8], L_GEN[4]);
  and and_17 (MOP1, not_38_out, L_GEN[4]);
  nor nor_1 (nor_1_out, IOT, L_GEN[4]);
  and and_18 (ZEROPAGE, IR[7], nor_1_out);
  and and_19 (INDIRECT, IR[8], nor_1_out);
  // Probe on AND
  // Probe on L_GEN[10]
  // Probe on ISZ
  // Probe on DCA
  // Probe on JMS
  // Probe on JMP
  // Probe on IOT
  // Probe on L_GEN[4]
  or or_30 (or_30_out, AND, L_GEN[10], DCA, JMP, JMS);
  or or_31 (ii, ii_mop1, ckACC_2, ii_jmp, ii_dca, ii_iot, ii_isz, ii_mop2, ii_jms, ii_mop3a);
  or or_32 (iDone, iDone1, RESET, ckIRQhandler);
  or or_33 (INC1, ii_dca, ckACC_2, ckACC_mop1, INC1_mop2, ckSetPC_jms, INC1_mop3a, INC1_iot, INC1_isz);
  or or_34 (INC2, INC2_mop2, INC2_isz, INC2_iot3, INC2_iot5, INC2_iot1, INC2_iot2, INC2_iot4);
  or or_35 (or_35_out, AND, L_GEN[10]);
  RS_FF_AS rs_ff_as_2 (.S(ii), .R(iDone), .Q(inhibitIR));  // open: nQ
  // Probe on iDone
  SequencerAI sequencerai_1 (
    .EN(or_30_out), .CLK(CLK_t), .fAI(fAutoinc), .DONE(ii), .P1a(enRAMtoDBUS_ai), .P1b(enINSTRtoABUS_ai),
    .P2(ckIncDBUS__ai), .P3a(weRAM_ai), .P3b(enIncToDBUS_ai), .Fin(aiFinished));
  and and_20 (and_20_out, aiFinished, or_35_out);
  and and_21 (and_21_out, aiFinished, DCA);
  and and_22 (and_22_out, aiFinished, JMP);
  and and_23 (and_23_out, aiFinished, JMS);
  Sequencer AND_TAD (
    .EN(and_20_out), .CLK(CLK_t), .DONE(ckACC_2), .D1(enRAMtoDBUS_andtad), .P1(AND_TAD_p1), .P2(AND_TAD_p2),
    .D3(AND_TAD_d3), .P3(AND_TAD_p3), .D4(AND_TAD_d4), .P4(AND_TAD_p4), .D5(AND_TAD_d5), .P5(AND_TAD_p5),
    .D6(AND_TAD_d6), .P6(AND_TAD_p6), .D7(enALUtoACC_andtad), .P7(AND_TAD_p7), .D8(ckACC_2));  // open: D2
  Sequencer u_DCA (
    .EN(and_21_out), .CLK(CLK_t), .DONE(ii_dca), .D1(DCA_d1), .P1(DCA_p1), .D2(DCA_d2), .P2(DCA_p2),
    .D3(DCA_d3), .P3(DCA_p3), .D4(DCA_d4), .P4(DCA_p4), .D5(DCA_d5), .P5(DCA_p5), .D6(enACCtoDBUS_dca),
    .P6(weRAM_dca), .D7(enACCclear_dca), .P7(DCA_p7), .D8(ii_dca));
  Sequencer JMP_JMPi (
    .EN(and_22_out), .CLK(CLK_t), .DONE(ii_jmp), .D1(enRAMtoDBUS_jmp), .P1(JMP_JMPi_p1), .D2(JMP_JMPi_d2),
    .P2(JMP_JMPi_p2), .D3(JMP_JMPi_d3), .P3(JMP_JMPi_p3), .D4(JMP_JMPi_d4), .P4(JMP_JMPi_p4),
    .D5(JMP_JMPi_d5), .P5(JMP_JMPi_p5), .D6(JMP_JMPi_d6), .P6(JMP_JMPi_p6), .D7(ckSetPC_jmp),
    .P7(JMP_JMPi_p7), .D8(ii_jmp));
  Sequencer JMS_JMSi (
    .EN(and_23_out), .CLK(CLK_t), .DONE(ii_jms), .D1(enRAMtoDBUS_jms), .P1(JMS_JMSi_p1), .D2(JMS_JMSi_d2),
    .P2(JMS_JMSi_p2), .D3(JMS_JMSi_d3), .P3(ckIncPC_jms1), .D4(JMS_JMSi_d4), .P4(ckSetPC_jms), .D5(ii_jms),
    .P5(JMS_JMSi_p5), .D6(JMS_JMSi_d6), .P6(JMS_JMSi_p6), .D7(JMS_JMSi_d7), .P7(JMS_JMSi_p7), .D8(JMS_JMSi_d8));
  Sequencer ISZ_ISZi (
    .EN(ISZ), .CLK(CLK_t), .DONE(ii_isz), .D1(ISZ_ISZi_d1), .P1(ISZ_ISZi_p1), .P2(ISZ_ISZi_p2),
    .P3(ISZ_ISZi_p3), .D4(ISZ_ISZi_d4), .P5(ckIncDBUS_isz1), .P6(enIncToDBUS_isz1), .P7(INC1_isz), .D8(ii_isz));  // open: D2, D3, P4, D5, D6, D7
  and and_24 (and_24_out, ~enIRQ, inhibitIR);  // And
  and and_25 (and_25_out, inhibitIR, enIRQ);
  Sequencer sequencer_1 (
    .EN(and_24_out), .CLK(CLK_t), .DONE(iDone1), .D1(enPCtoABUS_LoadIR), .P1(iDoneBeforeIRQ),
    .D2(sequencer_1_d2), .P2(ckIR_LoadIR), .D3(sequencer_1_d3), .P3(sequencer_1_p3), .D4(sequencer_1_d4),
    .P4(sequencer_1_p4), .D5(sequencer_1_d5), .P5(sequencer_1_p5), .D6(sequencer_1_d6), .P6(sequencer_1_p6),
    .D7(sequencer_1_d7), .P7(sequencer_1_p7), .D8(iDone1));
  Sequencer sequencer_2 (
    .EN(and_25_out), .CLK(CLK_t), .DONE(ckIRQhandler), .D1(sequencer_2_d1), .P1(weRAM_irq),
    .D2(sequencer_2_d2), .P2(sequencer_2_p2), .D3(sequencer_2_d3), .P3(clrPC_irq), .D4(enPCtoABUS_irq),
    .P4(sequencer_2_p4), .D5(sequencer_2_d5), .P5(ckIncPC_irq1), .D6(sequencer_2_d6), .P6(ckIR_irq),
    .D7(sequencer_2_d7), .P7(sequencer_2_p7), .D8(ckIRQhandler));
  and and_26 (and_26_out, JMP_JMPi_d2, ~fIndirect);  // And
  and and_27 (ckDBUStoABUS_jmp, JMP_JMPi_d2, fIndirect);
  or or_36 (or_36_out, enIncToDBUS_isz1, enIncToDBUS_isz2);
  or or_37 (or_37_out, sequencer_1_p3, weRAM_irq);
  and and_28 (and_28_out, enRAMtoDBUS_andtad, ~fIndirect);  // And
  and and_29 (enALUand, AND, enALUtoACC_andtad);
  and and_30 (enALUadd, L_GEN[10], enALUtoACC_andtad);
  and and_31 (and_31_out, DCA_d1, ~fIndirect);  // And
  or or_38 (enINSTRtoABUS_jmp, JMP_JMPi_p1, and_26_out);
  and and_32 (enRAMtoDBUS_isz, ISZ_ISZi_d1, ~or_36_out);  // And
  Delay #(.delayTime(20)) delay_9 (.in(iDoneBeforeIRQ), .out(delay_9_out));
  or or_39 (enINSTRtoABUS_andtad, and_28_out, AND_TAD_p1, AND_TAD_p2);
  and and_33 (ckDBUStoABUS_andtad, AND_TAD_p2, fIndirect);
  and and_34 (enDBUStoABUS_andtad, AND_TAD_d3, fIndirect);
  or or_40 (enRAMtoDBUS_dca, DCA_p1, DCA_p2, DCA_p3);
  or or_41 (enINSTRtoABUS_dca, and_31_out, DCA_p1, DCA_p2);
  and and_35 (ckDBUStoABUS_dca, DCA_p2, fIndirect);
  and and_36 (enDBUStoABUS_dca, DCA_d3, fIndirect);
  and and_37 (INC2_isz, INC1_isz, fDBUSisZero);
  OneShot oneshot_12 (.i(iDoneBeforeIRQ), .o(oneshot_12_o));
  OneShot oneshot_13 (.i(delay_9_out), .o(oneshot_13_o));
  RS_FF_AS rs_ff_as_3 (.S(INC1), .R(or_37_out), .Q(rs_ff_as_3_q));  // open: nQ
  RS_FF_AS rs_ff_as_4 (.S(INC2), .R(or_37_out), .Q(rs_ff_as_4_q));  // open: nQ
  and and_38 (and_38_out, JMS_JMSi_d2, ~fIndirect);  // And
  and and_39 (ckDBUStoABUS_jms, JMS_JMSi_d2, fIndirect);
  or or_42 (enPCtoDBUS_irq, weRAM_irq, sequencer_2_p2);
  or or_43 (enINSTRtoABUS_jms, JMS_JMSi_p1, and_38_out);
  and and_40 (and_40_out, ~fIndirect, ISZ_ISZi_d4);  // And
  and and_41 (ckDBUStoABUS_isz, ISZ_ISZi_d4, fIndirect);
  and and_42 (and_42_out, oneshot_12_o, rs_ff_as_3_q);
  and and_43 (and_43_out, oneshot_13_o, rs_ff_as_4_q);
  or or_44 (enINSTRtoABUS_isz, ISZ_ISZi_p1, ISZ_ISZi_p2, and_40_out, ISZ_ISZi_p3);
  and and_44 (ckIncDBUS__isz2, fAutoinc, ISZ_ISZi_p2);
  and and_45 (enIncToDBUS_isz2, fAutoinc, ISZ_ISZi_p3);
  or or_45 (ckIncPC_LoadIR, and_42_out, and_43_out);
  Sequencer u_MOP1 (
    .EN(MOP1), .CLK(CLK_t), .DONE(ii_mop1), .D1(enALUtoACC_mop1), .P1(MOP1_p1), .D2(ckACC_mop1),
    .P2(MOP1_p2), .D3(ii_mop1), .P3(MOP1_p3), .D4(MOP1_d4), .P4(MOP1_p4), .D5(MOP1_d5), .P5(MOP1_p5),
    .D6(MOP1_d6), .P6(MOP1_p6), .D7(MOP1_d7), .P7(MOP1_p7), .D8(MOP1_d8));
  Sequencer u_MOP2 (
    .EN(MOP2), .CLK(CLK_t), .DONE(ii_mop2), .D1(enPCtoABUS_mop2), .P1(MOP2_p1), .D2(MOP2_d2), .P2(INC1_mop2),
    .D3(enALUtoACC_mop2), .P3(MOP2_p3), .D4(MOP2_d4), .P4(MOP2_p4), .D5(MOP2_d5), .P5(MOP2_p5), .D6(ii_mop2),
    .P6(MOP2_p6), .D7(MOP2_d7), .P7(MOP2_p7), .D8(MOP2_d8));
  Sequencer u_MOP3 (
    .EN(MOP3), .CLK(CLK_t), .DONE(ii_mop3a), .D1(MOP3_d1), .P1(INC1_mop3a), .D2(MOP3_d2), .P2(MOP3_p2),
    .D3(MOP3_d3), .P3(MOP3_p3), .D4(ii_mop3a), .P4(MOP3_p4), .D5(MOP3_d5), .P5(MOP3_p5), .D6(MOP3_d6),
    .P6(MOP3_p6), .D7(MOP3_d7), .P7(MOP3_p7));  // open: D8
  not not_39 (not_39_out, IR[3]);
  not not_40 (not_40_out, IR[4]);
  not not_41 (not_41_out, IR[5]);
  not not_42 (not_42_out, IR[6]);
  and and_46 (IAC, MOP1, IR[0]);
  and and_47 (CML, MOP1, IR[4]);
  and and_48 (CMA, MOP1, IR[5]);
  and and_49 (CLL, MOP1, IR[6]);
  and and_50 (CLA_1, MOP1, IR[7]);
  or or_46 (or_46_out, L_OPR2[1], CLA_2);
  and and_51 (STOP, MOP2_d5, HLT);
  and and_52 (CODE_lsb, MOP3, IR[1]);
  and and_53 (CODE_mid, MOP3, IR[2]);
  and and_54 (CODE_msb, MOP3, IR[3]);
  and and_55 (MQL, MOP3, IR[4]);
  and and_56 (L_OPR3[10], MOP3, IR[5]);
  and and_57 (MQA, MOP3, IR[6]);
  and and_58 (CLA_3, MOP3, IR[7]);
  and and_59 (L_OPR3[9], MQA, MQL);
  _74LS238 _74ls238_10 (
    .A(IR[1]), .B(IR[2]), .C(IR[3]), .G(MOP1), .nGB(1'b0), .nGA(1'b0), .Y1(BSW), .Y2(L_OPR1[1]),
    .Y3(L_OPR1[2]), .Y4(L_OPR1[4]), .Y5(L_OPR1[3]));  // open: Y0, Y6, Y7
  and and_60 (HLT, MOP2, IR[1]);
  and and_61 (L_OPR2[1], MOP2, IR[2]);
  and and_62 (L_OPR2[2], MOP2, IR[3], IR[4]);
  and and_63 (L_OPR2[4], MOP2, IR[3], IR[5]);
  and and_64 (L_OPR2[5], MOP2, IR[3], IR[6]);
  and and_65 (L_OPR2[3], MOP2, not_39_out, IR[4]);
  and and_66 (L_OPR2[6], MOP2, not_39_out, IR[5]);
  and and_67 (L_OPR2[7], MOP2, not_39_out, IR[6]);
  and and_68 (CLA_2, MOP2, IR[7]);
  and and_69 (L_OPR2[8], MOP2, IR[3], not_40_out, not_41_out, not_42_out);
  and and_70 (INC2_mop2, INC1_mop2, fSkip);
  and and_71 (enALUor_mop2, enALUtoACC_mop2, L_OPR2[1]);
  and and_72 (ckACC_mop2, or_46_out, MOP2_p4);
  and and_73 (L_OPR3[7], MQL, ~MQA);  // And
  and and_74 (L_OPR3[8], ~MQL, MQA);  // And
  and and_75 (and_75_out, CLA, INC1_mop3a);
  and and_76 (ckMQ_1, MOP3_d2, L_OPR3[7]);
  and and_77 (and_77_out, L_OPR3[7], MOP3_p2);
  and and_78 (enACCtoDBUS_2, MOP3_d2, L_OPR3[8]);
  and and_79 (ckACC_4, L_OPR3[8], MOP3_p3);
  and and_80 (CLA_4, MOP3_d2, L_OPR3[9]);
  and and_81 (ckACC_5, L_OPR3[9], MOP3_p3);
  and and_82 (and_82_out, fAccIsZero, IR[5]);
  and and_83 (and_83_out, ACC11, IR[6]);
  and and_84 (and_84_out, LINK, IR[4]);
  or or_47 (or_47_out, and_82_out, and_83_out, and_84_out);
  or or_48 (enACCclear_mop3a, and_75_out, and_77_out);
  xor xor_1 (fSkip, or_47_out, IR[3]);
  Sequencer u_IOT (
    .EN(IOT), .CLK(CLK_t), .DONE(ii_iot), .D1(IOT_d1), .P1(INC1_iot), .D2(IOT_d2), .P2(IOT_p2), .D3(ii_iot),
    .P3(IOT_p3), .D4(IOT_d4), .P4(IOT_p4), .D5(IOT_d5), .P5(IOT_p5), .D6(IOT_d6), .P6(IOT_p6), .D7(IOT_d7),
    .P7(IOT_p7), .D8(IOT_d8));
  // Probe on L_CPU[7]
  // Probe on ION_6001
  // Probe on IOF_6002
  // Probe on L_CPU[4]
  // Probe on GTF_6004
  // Probe on L_CPU[2]
  // Probe on L_CPU[1]
  // Probe on CAF_6007
  // Probe on L_PRN[5]
  // Probe on L_PRN[4]
  // Probe on L_PRN[3]
  // Probe on L_PRN[2]
  // Probe on L_PRN[1]
  // Probe on L_PRN[0]
  // Probe on KCF_6030
  // Probe on KSF_6031
  // Probe on KCC_6032
  // Probe on KIE_6035
  // Probe on KRB_6036
  or or_49 (or_49_out, INC2_iot5, IOF_6002);
  or or_50 (or_50_out, fPRN, fKBD);
  and and_85 (INC2_iot5, L_CPU[7], fGIE, INC1_iot);
  and and_86 (and_86_out, ION_6001, INC1_iot);
  and and_87 (and_87_out, or_49_out, INC1_iot);
  and and_88 (INC2_iot4, L_CPU[4], fPendInt, INC1_iot);
  and and_89 (and_89_out, INC1_iot, GTF_6004);
  and and_90 (and_90_out, INC1_iot, L_CPU[2]);
  and and_91 (and_91_out, INC1_iot, L_CPU[1]);
  and and_92 (CAF, INC1_iot, CAF_6007);
  and and_93 (and_93_out, L_PRN[5], INC1_iot);
  and and_94 (INC2_iot2, L_PRN[4], fPRN, INC1_iot);
  and and_95 (and_95_out, L_PRN[3], INC1_iot);
  and and_96 (and_96_out, INC1_iot, L_PRN[2]);
  and and_97 (INC2_iot1, L_PRN[1], or_50_out, INC1_iot);
  and and_98 (and_98_out, L_PRN[0], INC1_iot);
  and and_99 (and_99_out, KCF_6030, INC1_iot);
  and and_100 (INC2_iot3, KSF_6031, fKBD, INC1_iot);
  and and_101 (enACCclear_iot1, KCC_6032, INC1_iot);
  and and_102 (and_102_out, KRS_6034, INC1_iot);
  and and_103 (KIE, KIE_6035, INC1_iot);
  and and_104 (KRB, KRB_6036, INC1_iot);
  and and_105 (and_105_out, KRB_6036, IOT_p2);
  or or_51 (or_51_out, and_86_out, RTF_INTEset);
  or or_52 (or_52_out, RTF_INTEclr, ckIRQhandler, RESET, and_87_out, CAF);
  not not_43 (not_43_out, and_89_out);
  not not_44 (not_44_out, and_89_out);
  or or_53 (or_53_out, KRB, and_102_out);
  not not_45 (not_45_out, not_44_out);
  not not_46 (not_46_out, not_45_out);
  or or_54 (enACCtoDBUS_tty, and_96_out, and_98_out);
  // Probe on iDoneBeforeIRQ
  RS_FF_AS INTE (.S(or_51_out), .R(or_52_out), .Q(fGIE), .nQ(INTE_nq));
  not not_47 (not_47_out, not_46_out);
  not not_48 (not_48_out, or_53_out);
  not not_49 (not_49_out, not_48_out);
  D_FF_AS d_ff_as_1 (.Set(1'b0), .D(1'b1), .C(iDoneBeforeIRQ), .Clr(INTE_nq), .Q(d_ff_as_1_q));  // open: nQ
  not not_50 (not_50_out, not_47_out);
  not not_51 (ckACC_gtf, not_50_out);
  or or_55 (or_55_out, and_99_out, enACCclear_iot1, RESET, KRB, CAF);
  not not_52 (not_52_out, not_49_out);
  not not_53 (ckACC_iot1, not_52_out);
  D_FF_AS d_ff_as_2 (
    .Set(1'b0), .D(d_ff_as_1_q), .C(iDoneBeforeIRQ), .Clr(INTE_nq), .Q(d_ff_as_2_q), .nQ(d_ff_as_2_nq));
  and and_106 (RTF_linkSet, and_90_out, ACC11);
  and and_107 (RTF_linkClr, and_90_out, ~ACC11);  // And
  and and_108 (RTF_INTEclr, and_90_out, ACC11);
  and and_109 (RTF_INTEset, and_90_out, ~ACC11);  // And
  or or_56 (or_56_out, and_93_out, tty_1_txdone);
  or or_57 (or_57_out, and_95_out, CAF, RESET, and_98_out);
  // Probe on enACCtoDBUS_tty
  RS_FF_AS PRN_FLAG (.S(or_56_out), .R(or_57_out), .Q(fPRN));  // open: nQ
  RS_FF_AS KBD_FLAG (.S(oneshot_14_o), .R(or_55_out), .Q(fKBD));  // open: nQ
  and and_110 (and_110_out, KIE, ACC11);
  and and_111 (and_111_out, KIE, ~ACC11);  // And
  and and_112 (enIRQ, d_ff_as_2_q, fPendInt, fGIE);
  and and_113 (fIrqDly, fGIE, d_ff_as_2_nq);
  // Probe on DAW[11:0]
  Delay #(.delayTime(5)) delay_10 (.in(enACCtoDBUS_tty), .out(delay_10_out));
  or or_58 (or_58_out, CAF, and_110_out);
  RS_FF_AS TTY_IE (.S(or_58_out), .R(and_111_out), .Q(TTY_IE_q));  // open: nQ
  and and_114 (and_114_out, TTY_IE_q, fPRN);
  TTY tty_1 (
    .ck(_100Hz), .Tx(DAW[11:0]), .TxTrig(delay_10_out), .RxAck(and_105_out), .RxEn(or_53_out),
    .TxDone(tty_1_txdone), .Rx(ALU_xout), .RxAvail(tty_1_rxavail));
  _74LS244 _74ls244_7 (
    ._1A1(1'b0), ._1A2(1'b0), ._1A3(1'b0), ._1A4(1'b0), ._1nG(not_43_out), ._2A1(1'b0), ._2A2(1'b0),
    ._2A3(1'b0), ._2A4(fGIE), ._2nG(not_43_out), ._1Y1(ALU_xout[0]), ._1Y2(ALU_xout[1]), ._1Y3(ALU_xout[2]),
    ._1Y4(ALU_xout[3]), ._2Y1(ALU_xout[4]), ._2Y2(ALU_xout[5]), ._2Y3(ALU_xout[6]), ._2Y4(ALU_xout[7]));
  _74LS244 _74ls244_8 (
    ._1A1(1'b0), ._1A2(fPendInt), ._1A3(1'b0), ._1A4(LINK), ._1nG(not_43_out), ._2A1(LINK), ._2A2(1'b0),
    ._2A3(1'b0), ._2A4(1'b0), ._2nG(not_43_out), ._1Y1(ALU_xout[8]), ._1Y2(ALU_xout[9]), ._1Y3(ALU_xout[10]),
    ._1Y4(ALU_xout[11]), ._2Y1(ALU_Lout));  // open: _2Y2, _2Y3, _2Y4
  // Probe on tty_1_txdone
  // Probe on ALU_xout
  and and_115 (and_115_out, tty_1_rxavail, _100Hz);
  or or_59 (fPendInt, and_114_out, fKBD);
  OneShot oneshot_14 (.i(and_115_out), .o(oneshot_14_o));
  nor nor_2 (nor_2_out, CLA_1, CLA_2, CLA_3, CLA_4);
  not not_54 (not_54_out, enALUand);
  or or_60 (or_60_out, DAW[0], not_54_out);
  or or_61 (or_61_out, DAW[1], not_54_out);
  or or_62 (or_62_out, DAW[2], not_54_out);
  or or_63 (or_63_out, DAW[3], not_54_out);
  or or_64 (or_64_out, DAW[4], not_54_out);
  or or_65 (or_65_out, DAW[5], not_54_out);
  or or_66 (or_66_out, DAW[6], not_54_out);
  or or_67 (or_67_out, DAW[7], not_54_out);
  or or_68 (or_68_out, DAW[8], not_54_out);
  or or_69 (or_69_out, DAW[9], not_54_out);
  or or_70 (or_70_out, DAW[10], not_54_out);
  or or_71 (or_71_out, DAW[11], not_54_out);
  not not_55 (CLA, nor_2_out);
  and and_116 (and_127_out[0], ACCC[0], or_60_out, nor_2_out);
  and and_117 (and_127_out[1], ACCC[1], or_61_out, nor_2_out);
  and and_118 (and_127_out[2], ACCC[2], or_62_out, nor_2_out);
  and and_119 (and_127_out[3], ACCC[3], or_63_out, nor_2_out);
  and and_120 (and_127_out[4], ACCC[4], or_64_out, nor_2_out);
  and and_121 (and_127_out[5], ACCC[5], or_65_out, nor_2_out);
  and and_122 (and_127_out[6], ACCC[6], or_66_out, nor_2_out);
  and and_123 (and_127_out[7], ACCC[7], or_67_out, nor_2_out);
  and and_124 (and_127_out[8], ACCC[8], or_68_out, nor_2_out);
  and and_125 (and_127_out[9], ACCC[9], or_69_out, nor_2_out);
  and and_126 (and_127_out[10], ACCC[10], or_70_out, nor_2_out);
  and and_127 (and_127_out[11], ACC11, or_71_out, nor_2_out);
  or or_72 (or_72_out, enALUor_mop2, enACCtoDBUS_2, CLA_4);
  and and_128 (and_128_out, OBUS[0], or_72_out);
  and and_129 (and_129_out, OBUS[1], or_72_out);
  and and_130 (and_130_out, OBUS[2], or_72_out);
  and and_131 (and_131_out, OBUS[3], or_72_out);
  and and_132 (and_132_out, OBUS[4], or_72_out);
  and and_133 (and_133_out, OBUS[5], or_72_out);
  and and_134 (and_134_out, OBUS[6], or_72_out);
  and and_135 (and_135_out, OBUS[7], or_72_out);
  and and_136 (and_136_out, OBUS[8], or_72_out);
  and and_137 (and_137_out, OBUS[9], or_72_out);
  and and_138 (and_138_out, OBUS[10], or_72_out);
  and and_139 (and_139_out, OBUS[11], or_72_out);
  or or_73 (or_84_out[0], and_127_out[0], and_128_out);
  or or_74 (or_84_out[1], and_127_out[1], and_129_out);
  or or_75 (or_84_out[2], and_127_out[2], and_130_out);
  or or_76 (or_84_out[3], and_127_out[3], and_131_out);
  or or_77 (or_84_out[4], and_127_out[4], and_132_out);
  or or_78 (or_84_out[5], and_127_out[5], and_133_out);
  or or_79 (or_84_out[6], and_127_out[6], and_134_out);
  or or_80 (or_84_out[7], and_127_out[7], and_135_out);
  or or_81 (or_84_out[8], and_127_out[8], and_136_out);
  or or_82 (or_84_out[9], and_127_out[9], and_137_out);
  or or_83 (or_84_out[10], and_127_out[10], and_138_out);
  or or_84 (or_84_out[11], and_127_out[11], and_139_out);
  and and_140 (and_151_out[0], DAW[0], enALUadd);
  and and_141 (and_151_out[1], DAW[1], enALUadd);
  and and_142 (and_151_out[2], DAW[2], enALUadd);
  and and_143 (and_151_out[3], DAW[3], enALUadd);
  and and_144 (and_151_out[4], DAW[4], enALUadd);
  and and_145 (and_151_out[5], DAW[5], enALUadd);
  and and_146 (and_151_out[6], DAW[6], enALUadd);
  and and_147 (and_151_out[7], DAW[7], enALUadd);
  and and_148 (and_151_out[8], DAW[8], enALUadd);
  and and_149 (and_151_out[9], DAW[9], enALUadd);
  and and_150 (and_151_out[10], DAW[10], enALUadd);
  and and_151 (and_151_out[11], DAW[11], enALUadd);
  xor xor_2 (xor_2_out, CMA, or_84_out[0]);
  xor xor_3 (xor_3_out, CMA, or_84_out[1]);
  xor xor_4 (xor_4_out, CMA, or_84_out[2]);
  xor xor_5 (xor_5_out, CMA, or_84_out[3]);
  xor xor_6 (xor_6_out, CMA, or_84_out[4]);
  xor xor_7 (xor_7_out, CMA, or_84_out[5]);
  xor xor_8 (xor_8_out, CMA, or_84_out[6]);
  xor xor_9 (xor_9_out, CMA, or_84_out[7]);
  xor xor_10 (xor_10_out, CMA, or_84_out[8]);
  xor xor_11 (xor_11_out, CMA, or_84_out[9]);
  xor xor_12 (xor_12_out, CMA, or_84_out[10]);
  xor xor_13 (xor_13_out, CMA, or_84_out[11]);
  _74LS283 _74ls283_4 (
    .A1(and_151_out[0]), .A2(and_151_out[1]), .A3(and_151_out[2]), .A4(and_151_out[3]), .B1(xor_2_out),
    .B2(xor_3_out), .B3(xor_4_out), .B4(xor_5_out), .S1(_74ls283_5_s4[0]), .S2(_74ls283_5_s4[1]),
    .S3(_74ls283_5_s4[2]), .S4(_74ls283_5_s4[3]), .C_in(IAC), .C_out(_74ls283_4_c_out));
  _74LS283 _74ls283_5 (
    .A1(and_151_out[4]), .A2(and_151_out[5]), .A3(and_151_out[6]), .A4(and_151_out[7]), .B1(xor_6_out),
    .B2(xor_7_out), .B3(xor_8_out), .B4(xor_9_out), .S1(_74ls283_5_s4[4]), .S2(_74ls283_5_s4[5]),
    .S3(_74ls283_5_s4[6]), .S4(_74ls283_5_s4[7]), .C_in(_74ls283_4_c_out), .C_out(_74ls283_5_c_out));
  _74LS283 _74ls283_6 (
    .A1(and_151_out[8]), .A2(and_151_out[9]), .A3(and_151_out[10]), .A4(and_151_out[11]), .B1(xor_10_out),
    .B2(xor_11_out), .B3(xor_12_out), .B4(xor_13_out), .S1(_74ls283_5_s4[8]), .S2(_74ls283_5_s4[9]),
    .S3(_74ls283_5_s4[10]), .S4(_74ls283_5_s4[11]), .C_in(_74ls283_5_c_out), .C_out(IAC_carryout));
  or or_85 (or_85_out, enALUtoACC_mop1, enALUtoACC_andtad, enALUtoACC_mop2, enACCtoDBUS_2, CLA_4);
  nand nand_1 (nand_1_out, BSW, or_85_out);
  nand nand_2 (nand_2_out, L_OPR1[1], or_85_out);
  nand nand_3 (nand_3_out, L_OPR1[2], or_85_out);
  nand nand_4 (nand_4_out, L_OPR1[4], or_85_out);
  nand nand_5 (nand_5_out, L_OPR1[3], or_85_out);
  nand nand_6 (nand_6_out, or_85_out, and_152_out);
  and and_152 (and_152_out, nand_1_out, nand_2_out, nand_3_out, nand_4_out, nand_5_out);
  _74LS541 _74ls541_5 (
    .nOE1(nand_6_out), .nOE2(nand_6_out), ._0D(_74ls283_5_s4[0]), ._1D(_74ls283_5_s4[1]),
    ._2D(_74ls283_5_s4[2]), ._3D(_74ls283_5_s4[3]), ._4D(_74ls283_5_s4[4]), ._5D(_74ls283_5_s4[5]),
    ._6D(_74ls283_5_s4[6]), ._7D(_74ls283_5_s4[7]), ._0O(_74ls541_5__7o[0]), ._1O(_74ls541_5__7o[1]),
    ._2O(_74ls541_5__7o[2]), ._3O(_74ls541_5__7o[3]), ._4O(_74ls541_5__7o[4]), ._5O(_74ls541_5__7o[5]),
    ._6O(_74ls541_5__7o[6]), ._7O(_74ls541_5__7o[7]));
  _74LS541 _74ls541_6 (
    .nOE1(nand_6_out), .nOE2(nand_6_out), ._0D(_74ls283_5_s4[8]), ._1D(_74ls283_5_s4[9]),
    ._2D(_74ls283_5_s4[10]), ._3D(_74ls283_5_s4[11]), ._4D(1'b0), ._5D(1'b0), ._6D(1'b0), ._7D(ALU_Lin),
    ._0O(_74ls541_6__3o[0]), ._1O(_74ls541_6__3o[1]), ._2O(_74ls541_6__3o[2]), ._3O(_74ls541_6__3o[3]),
    ._7O(_74ls541_6__7o));  // open: _4O, _5O, _6O
  _74LS541 _74ls541_7 (
    .nOE1(nand_1_out), .nOE2(nand_1_out), ._0D(_74ls283_5_s4[6]), ._1D(_74ls283_5_s4[7]),
    ._2D(_74ls283_5_s4[8]), ._3D(_74ls283_5_s4[9]), ._4D(_74ls283_5_s4[10]), ._5D(_74ls283_5_s4[11]),
    ._6D(_74ls283_5_s4[0]), ._7D(_74ls283_5_s4[1]), ._0O(_74ls541_5__7o[0]), ._1O(_74ls541_5__7o[1]),
    ._2O(_74ls541_5__7o[2]), ._3O(_74ls541_5__7o[3]), ._4O(_74ls541_5__7o[4]), ._5O(_74ls541_5__7o[5]),
    ._6O(_74ls541_5__7o[6]), ._7O(_74ls541_5__7o[7]));
  _74LS541 _74ls541_8 (
    .nOE1(nand_1_out), .nOE2(nand_1_out), ._0D(_74ls283_5_s4[2]), ._1D(_74ls283_5_s4[3]),
    ._2D(_74ls283_5_s4[4]), ._3D(_74ls283_5_s4[5]), ._4D(1'b0), ._5D(1'b0), ._6D(1'b0), ._7D(ALU_Lin),
    ._0O(_74ls541_6__3o[0]), ._1O(_74ls541_6__3o[1]), ._2O(_74ls541_6__3o[2]), ._3O(_74ls541_6__3o[3]),
    ._7O(_74ls541_6__7o));  // open: _4O, _5O, _6O
  _74LS541 _74ls541_9 (
    .nOE1(nand_2_out), .nOE2(nand_2_out), ._0D(ALU_Lin), ._1D(_74ls283_5_s4[0]), ._2D(_74ls283_5_s4[1]),
    ._3D(_74ls283_5_s4[2]), ._4D(_74ls283_5_s4[3]), ._5D(_74ls283_5_s4[4]), ._6D(_74ls283_5_s4[5]),
    ._7D(_74ls283_5_s4[6]), ._0O(_74ls541_5__7o[0]), ._1O(_74ls541_5__7o[1]), ._2O(_74ls541_5__7o[2]),
    ._3O(_74ls541_5__7o[3]), ._4O(_74ls541_5__7o[4]), ._5O(_74ls541_5__7o[5]), ._6O(_74ls541_5__7o[6]),
    ._7O(_74ls541_5__7o[7]));
  _74LS541 _74ls541_10 (
    .nOE1(nand_2_out), .nOE2(nand_2_out), ._0D(_74ls283_5_s4[7]), ._1D(_74ls283_5_s4[8]),
    ._2D(_74ls283_5_s4[9]), ._3D(_74ls283_5_s4[10]), ._4D(1'b0), ._5D(1'b0), ._6D(1'b0),
    ._7D(_74ls283_5_s4[11]), ._0O(_74ls541_6__3o[0]), ._1O(_74ls541_6__3o[1]), ._2O(_74ls541_6__3o[2]),
    ._3O(_74ls541_6__3o[3]), ._7O(_74ls541_6__7o));  // open: _4O, _5O, _6O
  _74LS541 _74ls541_11 (
    .nOE1(nand_3_out), .nOE2(nand_3_out), ._0D(_74ls283_5_s4[11]), ._1D(ALU_Lin), ._2D(_74ls283_5_s4[0]),
    ._3D(_74ls283_5_s4[1]), ._4D(_74ls283_5_s4[2]), ._5D(_74ls283_5_s4[3]), ._6D(_74ls283_5_s4[4]),
    ._7D(_74ls283_5_s4[5]), ._0O(_74ls541_5__7o[0]), ._1O(_74ls541_5__7o[1]), ._2O(_74ls541_5__7o[2]),
    ._3O(_74ls541_5__7o[3]), ._4O(_74ls541_5__7o[4]), ._5O(_74ls541_5__7o[5]), ._6O(_74ls541_5__7o[6]),
    ._7O(_74ls541_5__7o[7]));
  _74LS541 _74ls541_12 (
    .nOE1(nand_3_out), .nOE2(nand_3_out), ._0D(_74ls283_5_s4[6]), ._1D(_74ls283_5_s4[7]),
    ._2D(_74ls283_5_s4[8]), ._3D(_74ls283_5_s4[9]), ._4D(1'b0), ._5D(1'b0), ._6D(1'b0),
    ._7D(_74ls283_5_s4[10]), ._0O(_74ls541_6__3o[0]), ._1O(_74ls541_6__3o[1]), ._2O(_74ls541_6__3o[2]),
    ._3O(_74ls541_6__3o[3]), ._7O(_74ls541_6__7o));  // open: _4O, _5O, _6O
  _74LS541 _74ls541_13 (
    .nOE1(nand_4_out), .nOE2(nand_4_out), ._0D(_74ls283_5_s4[1]), ._1D(_74ls283_5_s4[2]),
    ._2D(_74ls283_5_s4[3]), ._3D(_74ls283_5_s4[4]), ._4D(_74ls283_5_s4[5]), ._5D(_74ls283_5_s4[6]),
    ._6D(_74ls283_5_s4[7]), ._7D(_74ls283_5_s4[8]), ._0O(_74ls541_5__7o[0]), ._1O(_74ls541_5__7o[1]),
    ._2O(_74ls541_5__7o[2]), ._3O(_74ls541_5__7o[3]), ._4O(_74ls541_5__7o[4]), ._5O(_74ls541_5__7o[5]),
    ._6O(_74ls541_5__7o[6]), ._7O(_74ls541_5__7o[7]));
  _74LS541 _74ls541_14 (
    .nOE1(nand_4_out), .nOE2(nand_4_out), ._0D(_74ls283_5_s4[9]), ._1D(_74ls283_5_s4[10]),
    ._2D(_74ls283_5_s4[11]), ._3D(ALU_Lin), ._4D(1'b0), ._5D(1'b0), ._6D(1'b0), ._7D(_74ls283_5_s4[0]),
    ._0O(_74ls541_6__3o[0]), ._1O(_74ls541_6__3o[1]), ._2O(_74ls541_6__3o[2]), ._3O(_74ls541_6__3o[3]),
    ._7O(_74ls541_6__7o));  // open: _4O, _5O, _6O
  _74LS541 _74ls541_15 (
    .nOE1(nand_5_out), .nOE2(nand_5_out), ._0D(_74ls283_5_s4[2]), ._1D(_74ls283_5_s4[3]),
    ._2D(_74ls283_5_s4[4]), ._3D(_74ls283_5_s4[5]), ._4D(_74ls283_5_s4[6]), ._5D(_74ls283_5_s4[7]),
    ._6D(_74ls283_5_s4[8]), ._7D(_74ls283_5_s4[9]), ._0O(_74ls541_5__7o[0]), ._1O(_74ls541_5__7o[1]),
    ._2O(_74ls541_5__7o[2]), ._3O(_74ls541_5__7o[3]), ._4O(_74ls541_5__7o[4]), ._5O(_74ls541_5__7o[5]),
    ._6O(_74ls541_5__7o[6]), ._7O(_74ls541_5__7o[7]));
  _74LS541 _74ls541_16 (
    .nOE1(nand_5_out), .nOE2(nand_5_out), ._0D(_74ls283_5_s4[10]), ._1D(_74ls283_5_s4[11]), ._2D(ALU_Lin),
    ._3D(_74ls283_5_s4[0]), ._4D(1'b0), ._5D(1'b0), ._6D(1'b0), ._7D(_74ls283_5_s4[1]),
    ._0O(_74ls541_6__3o[0]), ._1O(_74ls541_6__3o[1]), ._2O(_74ls541_6__3o[2]), ._3O(_74ls541_6__3o[3]),
    ._7O(_74ls541_6__7o));  // open: _4O, _5O, _6O
  or or_86 (or_86_out, enACCtoDBUS_dca, enACCtoDBUS_tty, enACCtoDBUS_2);
  // Probe on {_74ls541_6__3o, _74ls541_5__7o}
  or or_87 (or_87_out, enACCclear_dca, enACCclear_mop3a, RESET, CAF_6007, enACCclear_iot1);
  or or_88 (or_88_out, ckACC_mop1, ckACC_2, ckACC_mop2, ckACC_gtf, ckACC_4, ckACC_5, ckACC_iot1);
  or or_89 (or_89_out, CAF_6007, RESET, RTF_linkClr);
  or or_90 (or_90_out, enACCtoDBUS_2, CLA_4);
  not not_56 (not_56_out, CLA_4);
  or or_91 (or_91_out, ckMQ_1, ckACC_5);
  // Probe on {ACC11, ACCC}
  not not_57 (not_57_out, or_86_out);
  not not_58 (not_58_out, or_87_out);
  not not_59 (not_59_out, RTF_linkSet);
  not not_60 (not_60_out, or_89_out);
  not not_61 (not_61_out, or_90_out);
  _74LS273 _74ls273_9 (
    .CP(or_91_out), .nMR(nRESET), .D0(ACCC[0]), .D1(ACCC[1]), .D2(ACCC[2]), .D3(ACCC[3]), .D4(ACCC[4]),
    .D5(ACCC[5]), .D6(ACCC[6]), .D7(ACCC[7]), .Q0(_74ls273_9_q0), .Q1(_74ls273_9_q1), .Q2(_74ls273_9_q2),
    .Q3(_74ls273_9_q3), .Q4(_74ls273_9_q4), .Q5(_74ls273_9_q5), .Q6(_74ls273_9_q6), .Q7(_74ls273_9_q7));
  _74LS273 _74ls273_10 (
    .CP(or_91_out), .nMR(nRESET), .D0(ACCC[8]), .D1(ACCC[9]), .D2(ACCC[10]), .D3(ACC11), .D4(1'b0),
    .D5(1'b0), .D6(1'b0), .D7(1'b0), .Q0(_74ls273_10_q0), .Q1(_74ls273_10_q1), .Q2(_74ls273_10_q2),
    .Q3(_74ls273_10_q3));  // open: Q4, Q5, Q6, Q7
  _74LS273 _74ls273_11 (
    .CP(or_88_out), .nMR(not_58_out), .D0(_74ls541_5__7o[0]), .D1(_74ls541_5__7o[1]), .D2(_74ls541_5__7o[2]),
    .D3(_74ls541_5__7o[3]), .D4(_74ls541_5__7o[4]), .D5(_74ls541_5__7o[5]), .D6(_74ls541_5__7o[6]),
    .D7(_74ls541_5__7o[7]), .Q0(ACCC[0]), .Q1(ACCC[1]), .Q2(ACCC[2]), .Q3(ACCC[3]), .Q4(ACCC[4]),
    .Q5(ACCC[5]), .Q6(ACCC[6]), .Q7(ACCC[7]));
  _74LS273 _74ls273_12 (
    .CP(or_88_out), .nMR(not_58_out), .D0(_74ls541_6__3o[0]), .D1(_74ls541_6__3o[1]), .D2(_74ls541_6__3o[2]),
    .D3(_74ls541_6__3o[3]), .D4(1'b0), .D5(1'b0), .D6(1'b0), .D7(1'b0), .Q0(ACCC[8]), .Q1(ACCC[9]),
    .Q2(ACCC[10]), .Q3(ACC11));  // open: Q4, Q5, Q6, Q7
  _74LS74 _74ls74_5 (
    ._1nSD(not_59_out), ._1D(_74ls541_6__7o), ._1CP(or_88_out), ._1nRD(not_60_out), ._2nSD(1'b1), ._2D(1'b1),
    ._2CP(1'b1), ._2nRD(1'b1), ._1Q(LINK));  // open: _1nQ, _2Q, _2nQ
  _74LS373 _74ls373_1 (
    .Q0(MQ[0]), .Q1(MQ[1]), .Q2(MQ[2]), .Q3(MQ[3]), .Q4(MQ[4]), .Q5(MQ[5]), .Q6(MQ[6]), .Q7(MQ[7]),
    .nOC(1'b0), .C(not_56_out), .D0(_74ls273_9_q0), .D1(_74ls273_9_q1), .D2(_74ls273_9_q2),
    .D3(_74ls273_9_q3), .D4(_74ls273_9_q4), .D5(_74ls273_9_q5), .D6(_74ls273_9_q6), .D7(_74ls273_9_q7));
  _74LS373 _74ls373_2 (
    .Q0(MQ[8]), .Q1(MQ[9]), .Q2(MQ[10]), .Q3(MQ[11]), .nOC(1'b0), .C(not_56_out), .D0(_74ls273_10_q0),
    .D1(_74ls273_10_q1), .D2(_74ls273_10_q2), .D3(_74ls273_10_q3), .D4(1'b0), .D5(1'b0), .D6(1'b0), .D7(1'b0));  // open: Q4, Q5, Q6, Q7
  not not_62 (not_62_out, CLL);
  and and_153 (and_153_out, LINK, not_62_out);
  xor xor_14 (xor_14_out, and_153_out, CML);
  _74LS541 _74ls541_17 (
    .nOE1(not_61_out), .nOE2(not_61_out), ._0D(MQ[0]), ._1D(MQ[1]), ._2D(MQ[2]), ._3D(MQ[3]), ._4D(MQ[4]),
    ._5D(MQ[5]), ._6D(MQ[6]), ._7D(MQ[7]), ._0O(OBUS[0]), ._1O(OBUS[1]), ._2O(OBUS[2]), ._3O(OBUS[3]),
    ._4O(OBUS[4]), ._5O(OBUS[5]), ._6O(OBUS[6]), ._7O(OBUS[7]));
  _74LS541 _74ls541_18 (
    .nOE1(not_61_out), .nOE2(not_61_out), ._0D(MQ[8]), ._1D(MQ[9]), ._2D(MQ[10]), ._3D(MQ[11]), ._4D(1'b0),
    ._5D(1'b0), ._6D(1'b0), ._7D(1'b0), ._0O(OBUS[8]), ._1O(OBUS[9]), ._2O(OBUS[10]), ._3O(OBUS[11]));  // open: _4O, _5O, _6O, _7O
  _74LS541 _74ls541_19 (
    .nOE1(not_57_out), .nOE2(not_57_out), ._0D(ACCC[0]), ._1D(ACCC[1]), ._2D(ACCC[2]), ._3D(ACCC[3]),
    ._4D(ACCC[4]), ._5D(ACCC[5]), ._6D(ACCC[6]), ._7D(ACCC[7]), ._0O(DAW[0]), ._1O(DAW[1]), ._2O(DAW[2]),
    ._3O(DAW[3]), ._4O(DAW[4]), ._5O(DAW[5]), ._6O(DAW[6]), ._7O(DAW[7]));
  _74LS541 _74ls541_20 (
    .nOE1(not_57_out), .nOE2(not_57_out), ._0D(ACCC[8]), ._1D(ACCC[9]), ._2D(ACCC[10]), ._3D(ACC11),
    ._4D(1'b0), ._5D(1'b0), ._6D(1'b0), ._7D(1'b0), ._0O(DAW[8]), ._1O(DAW[9]), ._2O(DAW[10]), ._3O(DAW[11]));  // open: _4O, _5O, _6O, _7O
  xor xor_15 (ALU_Lin, xor_14_out, IAC_carryout);
  // Probe on {ACC11, ACCC}
  // Probe on DAW[11:0]
  // Probe on OBUS
  or or_92 (or_92_out, ACCC[0], ACCC[1], ACCC[2], ACCC[3], ACCC[4], ACCC[5], ACCC[6], ACCC[7], ACCC[8], ACCC[9], ACCC[10], ACC11);
  not not_63 (fAccIsZero, or_92_out);

  // Other names for the same wires on the sheet: DAW[23:12] = ABUS; ACCC[11] = ACC11; DBUS[11:0] = DAW[11:0];
  //   L_GEN (some bits) = {AND, ISZ, DCA, JMS, JMP, IOT, fIndirect, fAutoinc, isCurrPage}; IR0__6[6:0] = IR[6:0];
  //   OPR_TSTINV = IR[3]; OPR_SNLSZL = IR[4]; OPR_SZASNA = IR[5]; OPR_SMASPA = IR[6];
  //   L_OPR1 (some bits) = {CLA_1, CLL, CMA, CML, IAC, BSW};
  //   L_CPU (some bits) = {ION_6001, IOF_6002, GTF_6004, CAF_6007}; INC1_mop1 = ckACC_mop1; ckMQ_2 = ckACC_5;
  //   INC1_jms = ckSetPC_jms; L_OPR2 (some bits) = {CLA_2, HLT}; L_OPR3[11] = CLA_3;
  //   enDBUStoABUS_isz = ckDBUStoABUS_isz; enDBUStoABUS_jmp = ckDBUStoABUS_jmp; enDBUStoABUS_jms = ckDBUStoABUS_jms;
  //   L_IRQ (some bits) = {fGIE, fIrqDly, enIRQ, fKBD, fPRN}; enKEYtoDBUS_2 = enDBUStoABUS_0;
  //   enALUor_2 = enACCtoDBUS_2; enALUtoACC_4 = enACCtoDBUS_2; enMQtoOBUS_1 = enACCtoDBUS_2; enALUor_3 = CLA_4;
  //   enALUtoACC_5 = CLA_4; enMQhold = CLA_4; enMQtoOBUS_2 = CLA_4; enPCtoABUS_rim = enKEYtoDBUS_0;
  //   enRAMtoDBUS_0 = enPCtoABUS_0; enRAMtoDBUS_irq = enPCtoABUS_irq; enRAMtoDBUS_LoadIR = enPCtoABUS_LoadIR;
  //   enSwitchToOBUS = enALUor_mop2; iDone2 = ckIRQhandler; ii_andtad = ckACC_2; INC1_tadand = ckACC_2;
  //   INC1_dca = ii_dca; L_KBD[5:0] = {KCF_6030, KSF_6031, KCC_6032, KRS_6034, KIE_6035, KRB_6036};
  //   LED_MQA = L_OPR3[8]; LED_MQL = L_OPR3[7]; LED_SWP = L_OPR3[9]; MOP = L_GEN[4]; OSR = L_OPR2[1]; RAL = L_OPR1[1];
  //   RAR = L_OPR1[4]; RTF_6005 = L_CPU[2]; RTL = L_OPR1[2]; RTR = L_OPR1[3]; SCA = L_OPR3[10]; SGT_6006 = L_CPU[1];
  //   SKON_6000 = L_CPU[7]; SKP = L_OPR2[8]; SMA = L_OPR2[7]; SNA = L_OPR2[4]; SNL = L_OPR2[3]; SPA = L_OPR2[5];
  //   SRQ_6003 = L_CPU[4]; SZA = L_OPR2[6]; SZL = L_OPR2[2]; TAD = L_GEN[10]; TCF_6042 = L_PRN[3];
  //   TFL_6040 = L_PRN[5]; TLS_6046 = L_PRN[0]; TPC_6044 = L_PRN[2]; TSF_6041 = L_PRN[4]; TSK_6045 = L_PRN[1];
  //   weRAM_isz1 = enIncToDBUS_isz1; weRAM_isz2 = enIncToDBUS_isz2; enPCtoDBUS_jms = ckIncPC_jms1;
  //   weRAM_jms = ckIncPC_jms1

  // Notes on the sheet:
  //   MAX: Hz: 2147483647
  //   _100Hz: Hz: 10
  //   clk: Hz: 1000
  //   AUTO RIM LOADER
  //   LOAD
  //   7756 6014
  //   7757 6011
  //   7760 5357
  //   7761 6016
  //   7762 7106
  //   7763 7006
  //   7764 7510
  //   7765 5357
  //   7766 7006
  //   7767 6011
  //   7770 5367
  //   7771 6016
  //   7772 7420
  //   7773 3776
  //   7774 3376
  //   7775 5357
  //   7776 0000
  //   7777 0000
  //   RAM (2 BUS)
  //   DBUS ADDER (1 BUS)
  //   BREAKPOINT
  //   KEYPAD
  //   RUN/STEP CLOCK
  //   BUTTONS
  //   RUN
  //   HALT
  //   STEP
  //   TRACE
  //   μSTEP
  //   PC
  //   DEPOSIT
  //   INCREMENT
  //   SWITCH
  //   CLEAR
  //   contents of eeprom_1 (hex, n*v repeats v):
  //   0,a01,2,3,0,0,f02,e00,0,7*f02,0,1,2,3,4,6,8,c,10,18,20,30,40,60
  //   ,80,c0,100,180,200,29c,300,400,600,6ca,800,fcf,ffe,ffd,ffb,ff7
  //   ,fef,fdf,e7f,fbf,f7f,eff,dff,bff,7ff,fff,aaa,555,c00,e00,f00,f80
  //   ,fe0,ff0,ff8,ffc,7,37,f,1f,3f,7f,ff,1ff,3ff,fc0,a95,56a,1f8,e07
  //   ,87,b05,a60,17*f02,237,e80,f02,f08,f02,e80,f20,f02,f28,f08,f02
  //   ,e80,228,f20,f08,f02,f28,f02,e80,225,f20,f08,f02,f28,f02,e00,e00
  //   ,f08,a64,e80,222,f20,f08,f02,f28,f02,e80,220,f20,f08,f02,f28,f02
  //   ,e80,21e,f20,f08,f02,f28,f02,e80,21c,f20,f08,f02,f28,f02,e80,21a
  //   ,f20,f08,f02,f28,f02,e80,218,f20,f08,f02,f28,f02,e80,216,f20,f08
  //   ,f02,f28,f02,e80,214,f20,f08,f02,f28,f02,e80,212,f20,f08,f02,f28
  //   ,f02,e80,211,f20,f08,f02,f28,f02,e80,236,f48,f02,e80,228,f48,f08
  //   ,f02,e80,236,f40,f08,f02,e80,228,f40,f02,e80,237,e20,f20,f02,e80
  //   ,239,e20,f28,f02,239,e20,f20,f02,e80,238,e20,f28,f02,238,e20,f20
  //   ,f02,e80,237,e20,f20,f02,e80,e01,f20,f08,f02,e80,237,e01,f20,f02
  //   ,e80,241,4*e01,f20,f02,e80,e40,e04,f18,f02,e80,e40,e10,228,e04
  //   ,f18,f08,f02,e80,e40,e04,f10,f08,f02,e80,e40,e10,228,e04,f10,f02
  //   ,e80,228,e04,f10,aaa,e40,f18,f02,aae,e10,f10,f02,aa6,e40,f18,f02
  //   ,e10,f10,f02,e10,f18,f02,e80,237,f80,f20,f02,e80,f04,e20,f20,f02
  //   ,e80,e40,e00,f28,f18,f02,e80,e40,f00,f28,f18,f02,e80,236,228,e20
  //   ,f20,f02,e80,235,225,e20,f20,f02,e80,234,222,e20,f20,f02,e80,233
  //   ,220,e20,f20,f02,e80,232,21e,e20,f20,f02,e80,231,21c,e20,f20,f02
  //   ,e80,22f,21a,e20,f20,f02,e80,22e,218,e20,f20,f02,e80,22d,216,e20
  //   ,f20,f02,e80,22c,214,e20,f20,f02,e80,22b,212,e20,f20,f02,e80,22a
  //   ,211,e20,f20,f02,e80,e40,228,228,f18,f20,f02,e80,e40,23a,225,f18
  //   ,f20,f02,e80,e40,23b,222,f18,f20,f02,e80,e40,23c,220,f18,f20,f02
  //   ,e80,e40,23d,21e,f18,f20,f02,e80,e40,24b,21c,f18,f20,f02,e80,e40
  //   ,23e,21a,f18,f20,f02,e80,e40,23f,218,f18,f20,f02,e80,e40,240,216
  //   ,f18,f20,f02,e80,e40,241,214,f18,f20,f02,e80,e40,22a,212,f18,f20
  //   ,f02,e80,e40,237,211,f18,f20,f02,e80,e40,e10,228,228,f10,f20,f02
  //   ,e80,e40,236,225,225,e20,f10,f20,f02,e80,e40,235,222,222,e20,f10
  //   ,f20,f02,e80,e40,234,220,220,e20,f10,f20,f02,e80,e40,233,21e,21e
  //   ,e20,f10,f20,f02,e80,e40,232,21c,21c,e20,f10,f20,f02,e80,e40,231
  //   ,21a,21a,e20,f10,f20,f02,e80,e40,22f,218,218,e20,f10,f20,f02,e80
  //   ,e40,22e,216,216,e20,f10,f20,f02,e80,e40,22d,214,214,e20,f10,f20
  //   ,f02,e80,e40,22c,212,212,e20,f10,f20,f02,e80,e40,22b,211,211,e20
  //   ,f10,f18,f02,e80,e40,211,213,22c,e20,f10,f20,f02,e80,e40,212,215
  //   ,22d,e20,f10,f20,f02,e80,e40,214,217,22e,e20,f10,f20,f02,e80,e40
  //   ,216,219,22f,e20,f10,f20,f02,e80,e40,218,21b,231,e20,f10,f20,f02
  //   ,e80,e40,21a,21d,232,e20,f10,f20,f02,e80,e40,21c,21f,233,e20,f10
  //   ,f20,f02,e80,e40,21e,221,234,e20,f10,f20,f02,e80,e40,220,224,235
  //   ,e20,f10,f20,f02,e80,e40,222,226,236,e20,f10,f20,f02,e80,e40,225
  //   ,23a,f18,f20,f02,e80,e40,237,211,f18,f20,f02,e80,e40,213,213,240
  //   ,211,e20,f10,f20,f02,e80,e40,215,215,23f,213,e20,f10,f20,f02,e80
  //   ,e40,217,217,23e,242,e20,f10,f20,f02,e80,e40,219,219,229,e20,f10
  //   ,f20,f02,e80,e40,21b,21b,23d,245,e20,f10,f20,f02,e80,e40,21d,21d
  //   ,23c,246,e20,f10,f20,f02,e80,e40,21f,21f,230,e20,f10,f20,f02,e80
  //   ,e40,221,221,23a,248,e20,f10,f20,f02,e80,e40,224,224,228,249,e20
  //   ,f10,f20,f02,e80,e40,226,226,24a,e20,f10,f20,f02,e80,e40,23a,23a
  //   ,236,e20,f18,f20,f02,e80,e40,237,237,211,e20,f18,f20,f02,e80,e40
  //   ,211,e08,f10,f02,e80,e40,210,e08,f20,f02,e80,e40,210,e08,f18,f02
  //   ,e80,e40,e10,210,e08,f18,f02,e80,e40,e10,237,e08,e20,f20,f02,e80
  //   ,e40,e10,210,e08,236,e20,f28,f18,f02,e80,e40,228,e08,235,e20,f28
  //   ,f18,f02,e80,e40,225,e08,234,e20,f28,f18,f02,e80,e40,222,e08,233
  //   ,e20,f28,f18,f02,e80,e40,220,e08,232,e20,f28,f18,f02,e80,e40,21e
  //   ,e08,231,e20,f28,f18,f02,e80,e40,21c,e08,22f,e20,f28,f18,f02,e80
  //   ,e40,21a,e08,22e,e20,f28,f18,f02,e80,e40,218,e08,22d,e20,f28,f18
  //   ,f02,e80,e40,216,e08,22c,e20,f28,f18,f02,e80,e40,214,e08,22b,e20
  //   ,f28,f18,f02,e80,e40,212,e08,22a,e20,f28,f18,f02,e80,e40,211,e08
  //   ,237,e20,f28,f10,f02,e80,e40,212,e0a,f10,f02,e80,e40,210,e0a,f20
  //   ,f02,e80,e40,210,e0a,f18,f02,e80,e40,e10,210,e0a,f18,f02,e80,e40
  //   ,e10,237,e0a,e20,f20,f02,e80,e40,e10,210,e0a,235,e20,f28,f18,f02
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  //   DBUS->ABUS LATCH (2 BUS)
  //   ADDRESS FROM INSTRUCTION (2 BUS)
  //   INSTRUCTION REGISTER
  //   DISPLAY
  //   OPCODES
  //   INTERRUPT FLAGS
  //   OPR-4
  //   OPR-5
  //   OPR-6
  //   IOT-CPU
  //   IOT-KEYBOARD
  //   IOT-PRINTER
  //   contents of CharRom3x (hex, n*v repeats v):
  //   128*483f24cc03cf,128*1483f24cc03cf,128*2483f24cc03cf,128*3483f24cc03cf
  //   ,128*483f03cf4803,128*1483f03cf4803,128*2483f03cf4803,128*3483f03cf4803
  //   ,128*903303bb4833,128*1903303bb4833,128*2903303bb4833,128*3903303bb4833
  //   ,128*3cf00f3483f,128*103cf00f3483f,128*203cf00f3483f,128*303cf00f3483f
  //   ,128*3bb14cc007c,128*103bb14cc007c,128*203bb14cc007c,128*303bb14cc007c
  //   ,128*3c714cc007c,128*103c714cc007c,128*203c714cc007c,128*303c714cc007c
  //   ,513*480300ff4833,257*3c700ff14cc,0,253*3c700ff14cc
  //   TAD
  //   AND
  //   GIE
  //   IRQ
  //   IHBT
  //   CLA
  //   NOP
  //   SKP
  //   ION
  //   SKON
  //   KSF
  //   KCF
  //   TSF
  //   TFL
  //   ISZ
  //   IRQ
  //   DLY
  //   CLL
  //   SMA
  //   SCA
  //   IOF
  //   KCC
  //   TCF
  //   DCA
  //   INT
  //   BUS
  //   CMA
  //   SZA
  //   SWP
  //   SRQ
  //   KRS
  //   TPC
  //   JMS
  //   JMP
  //   TTY
  //   IE
  //   KEY
  //   AVAIL
  //   IAC
  //   CML
  //   SNA
  //   SPA
  //   MQA
  //   MQL
  //   RTF
  //   GTF
  //   KIE
  //   KRB
  //   TSK
  //   TLS
  //   PROGRAM COUNTER
  //   IOT
  //   PRN
  //   RDY
  //   RAR
  //   SNL
  //   LSR
  //   SGT
  //   OPR
  //   RTR
  //   SZL
  //   ASL
  //   CAF
  //   DIR
  //   IND
  //   RAL
  //   RTL
  //   OSR
  //   HLT
  //   SHL
  //   NMI
  //   INSTRUCTIONS PER SECOND
  //   AUTO
  //   IND
  //   BSW
  //   DVI
  //   CURR
  //   PAGE
  //   MUY
  //   SCL
  //   MQ
  //   IR
  //   ACC
  //   ABUS
  //   DBUS
  //   OBUS
  //   INSTRUCTION DECODER
  //   GRP3 msb1 & lsb1
  //   GRP2 msb1 & lsb0
  //   GRP1 msb0
  //   IR LOAD & PC INCREMENTER
  //   AUTO INDEXER
  //   INSTRUCTION SEQUENCING
  //   AND/ADD Accumulator
  //   deposit and clear AC
  //   increment and skip if zero
  //   MOP DECODER
  //   MOP
  //   Keyboard Flag
  //   The keyboard flag bit is set when a character has been read into the keyboard buffer. The console-reset or 
  //   power-on operation clears this flag. If interrupts are enabled, this flag generates an interrupt request when set.
  //   Teleprinter Flag
  //   The teleprinter flag bit is set when the character most recently loaded in the teleprinter buffer has been output. 
  //   The console-reset or power-on operation clears this flag. If interrupts are enabled, this flag generates an interrupt 
  //   request when set.
  //   -------------------------------------------------------------------------------------------------------------------------------------------------
  //   6000 - SKON Skip if Interrupt System On
  //   SKON is used to test the state of the interrupt enable flipflop. If interrupts are enabled, the next instruction in sequence is skipped.
  //   6001 - ION Interrupts On
  //   ION is used to turn on interrupts. The effect of this instruction is delayed one instruction so that, for example, an ION instruction 
  //   immediately before a return instruction will not take effect until the return instruction is executed.
  //   6002 - IOF Interrupts Off
  //   IOF is used to turn off or disable interrupts. The effect of this instruction is immediate. In addition, interrupts are disabled immediately 
  //   when an interrupt occurs.
  //   6003 - SRQ Skip on Interrupt Request
  //   SRQ is used to test whether there is a pending interrupt request. If a request is pending, the next instruction in sequence is skipped. 
  //   This test is only meaningful when interrupts are disabled; it may be used, for example, to avoid the expense of an unnecessary return 
  //   from interrupt when some device other than the one just serviced is also requesting service.
  //   6004 - GTF Get Flags
  //   GTF is similar to RIB, but is only available on the PDP-8/E and later models. 
  //   GTF loads the accumulator with various information that may need to be saved and restored during interrupts. 
  //   This includes the link bit, the state of the optional memory management unit, and the greater-than flag from 
  //   the optional extended arithmetic unit. These are packed into the accumulator in the following format:
  //   LINK- the link bit.
  //   GT - the Greater Than bit (see the SGT instruction supported by the extended arithmetic element.
  //   IR - the interrupt request status, as tested by SRQ. This is set to one if an interrupt requesting is pending.
  //   II - the interrupt inhibit bit associated with the Time-Share option of the memory management unit.
  //   IE - the state of the interrupt enable flipflop, as set by the ION and reset by the IOF instructions. This is set to one if interrupts are enabled.
  //   U - the user-mode bit.
  //   IF - the instruction field.
  //   DF - the data field. 
  //   U, IF and DF are the same as the corresponding fields returned by the RIB instruction.
  //   6005 - RTF Restore Flags
  //   RTF restores the state of the flags that are saved by the GTF instruction, using the same data format. 
  //   RTF ignores the IR (interrupt request) bit that was saved by GTF, and the IE (interrupt enable) bit is not fully restored until the 
  //   instruction after the RTF instruction, so that a return from interrupt may be executed before the next interrupt request is serviced.
  //   6006 - SGT Skip if Greater Than
  //   SGT is only supported if the extended arithmetic element is present, This instruction skips if the greater than flag is set.
  //   6007 - CAF Clear All Flags
  //   The effect of the CAF instruction is identical to a master clear issued from the front panel. AC and LINK are cleared, interrupts 
  //   are disabled globally, and all I/O devices are reset. Generally, resetting a device sets the device specific interrupt enable bit 
  //   and terminates any ongoing I/O activity. 
  //   -------------------------------------------------------------------------------------------------------------------------------------------------
  //   6030 - KCF Keyboard Clear Flags
  //   The keyboard flag, signalling input data ready, is cleared.
  //   6031 - KSF Keyboard Skip if Flag
  //   If the keyboard flag is set, indicating that input data is ready, the next instruction in sequence is skipped. 
  //   6032 - KCC Keyboard Clear and read character
  //   The keyboard flag is reset, the accumulator is cleared, and the process of reading the next character of input 
  //   is initiated (in those cases where the interface is connected to a paper-tape reader).
  //   6034 - KRS Keyboard Read Static
  //   The 8-bit character in the keyboard buffer is ored with the accumulator.
  //   6035 - KIE Keyboard Interrupt Enable
  //   The accumulator is loaded into the device control register (the interrupt enable and status report control bits). 
  //   6036 - KRB Keyboard Read and begin next read
  //   The 8 bit character in the keyboard buffer is transferred to the accumulator, and the keyboard flag is cleared, 
  //   allowing the reading of the next character to begin. In effect, this operation combines the KCC and KRS operations.
  //   -------------------------------------------------------------------------------------------------------------------------------------------------
  //   6040 - TFL Teleprinter Flag set
  //   The printer flag, signalling output complete, is set. 
  //   6041 - TSF Teleprinter Skip if Flag
  //   If the printer flag is set, indicating output is complete, the next instruction in sequence is skipped. 
  //   6042 - TCF Teleprinter Clear Flag
  //   The printer flag is reset.
  //   6044 - TPC Teleprinter Print Character
  //   The least significant 8-bits of the accumulator is copied to the print buffer, initiating output.
  //   6045 - TSK Teleprinter Skip
  //   If either the print flag or the keyboard flag are set, the next instruction in sequence is skipped. 
  //   6046 - TLS Teleprinter Load and start
  //   The least significant 8 bits of the accumulator are copied to the print buffer, initiating output, and the printer flag is reset. 
  //   In effect, this operation combines the TCF and TPC operations.
  //   MOPGRP1
  //   NOP/CLR
  //   load MQ from AC then clear AC
  //   inclusive OR the MQ with the AC
  //   AC=0
  //   AC negative
  //   LINK<>0
  //   SMA      7500  skip on minus AC
  //   SPA      7510  skip on plus AC
  //   SZA      7440  skip on zero AC
  //   SNA      7450  skip on non-zero AC
  //   SNL      7420  skip on non-zero link
  //   SZL      7430  skip on zero link
  //   IOT - CPU IRQ
  //   IOT - TELEPRINTER
  //   IOT - KEYBOARD
  //   ALU - AND & CLEAR (3)
  //   ALU - OR (3)
  //   ALU - INVERT & ADD (3)
  //   ADD
  //   IAC
  //   ALU - ROTATE/SWAP (2)
  //   PASSTHRU
  //   SWAP
  //   ROT L1
  //   ROT L2
  //   ROT R1
  //   ROT R2
  //   ACCUMULATOR/LINK/MQ (3)
endmodule
