// Digital circuit RAMSPY.dig as structural Verilog
module RAMSPY (
  input  [11:0] Trig,
  input  [24:0] DAW,
  output [11:0] O
);

  wire and_1_out, comparator_1_eq, delay_1_out;

  Comparator #(.Bits(12)) comparator_1 (.a(DAW[23:12]), .b(Trig), .eq(comparator_1_eq));  // open: gt, lt
  and and_1 (and_1_out, DAW[24], comparator_1_eq);
  Delay #(.delayTime(5)) delay_1 (.in(and_1_out), .out(delay_1_out));
  Register #(.Bits(12)) register_1 (.D(DAW[11:0]), .C(delay_1_out), .en(1'b1), .Q(O));

  // Notes on the sheet:
  //   RAM-DATA(12)
  //   RAM-ADDRESS(12)
  //   RAM_WE
endmodule
