// Digital circuit Sequencer.dig as structural Verilog
module Sequencer (
  input  EN,
  input  CLK,
  input  DONE,
  output D1,
  output P1,
  output D2,
  output P2,
  output D3,
  output P3,
  output D4,
  output P4,
  output D5,
  output P5,
  output D6,
  output P6,
  output D7,
  output P7,
  output D8
);

  wire and_1_out, d_ff_as_1_q, not_1_out, not_2_out, not_3_out, not_4_out, not_5_out, not_6_out, not_7_out,
       not_8_out, not_9_out, or_1_out;

  not not_1 (not_1_out, EN);
  D_FF_AS d_ff_as_1 (.Set(1'b0), .D(1'b1), .C(EN), .Clr(DONE), .Q(d_ff_as_1_q));  // open: nQ
  or or_1 (or_1_out, DONE, not_1_out);
  and and_1 (and_1_out, CLK, d_ff_as_1_q);
  not not_2 (not_2_out, or_1_out);
  _74LS273 _74ls273_1 (
    .D0(1'b1), .D1(D1), .D2(D2), .D3(D3), .D4(D4), .D5(D5), .D6(D6), .D7(D7), .CP(and_1_out),
    .nMR(not_2_out), .Q0(D1), .Q1(D2), .Q2(D3), .Q3(D4), .Q4(D5), .Q5(D6), .Q6(D7), .Q7(D8));
  not not_3 (not_3_out, D2);
  not not_4 (not_4_out, D3);
  not not_5 (not_5_out, D4);
  not not_6 (not_6_out, D5);
  not not_7 (not_7_out, D6);
  not not_8 (not_8_out, D7);
  not not_9 (not_9_out, D8);
  and and_2 (P1, D1, not_3_out);
  and and_3 (P2, D2, not_4_out);
  and and_4 (P3, D3, not_5_out);
  and and_5 (P4, D4, not_6_out);
  and and_6 (P5, D5, not_7_out);
  and and_7 (P6, D6, not_8_out);
  and and_8 (P7, D7, not_9_out);
endmodule
