// Digital circuit SequencerAI.dig as structural Verilog
module SequencerAI (
  input  EN,
  input  CLK,
  input  fAI,
  input  DONE,
  output P1a,
  output P1b,
  output P2,
  output P3a,
  output P3b,
  output Fin
);

  wire _74ls273_1_q0, _74ls273_1_q1, _74ls273_1_q2, _74ls273_1_q3, and_1_out, and_2_out, and_4_out,
       d_ff_as_1_q, not_1_out, not_2_out, not_3_out, not_4_out, not_5_out, not_6_out, or_1_out, or_2_out,
       or_3_out;

  not not_1 (not_1_out, EN);
  D_FF_AS d_ff_as_1 (.Set(1'b0), .D(1'b1), .C(EN), .Clr(DONE), .Q(d_ff_as_1_q));  // open: nQ
  or or_1 (or_1_out, DONE, not_1_out);
  and and_1 (and_1_out, CLK, fAI, d_ff_as_1_q);
  not not_2 (not_2_out, or_1_out);
  not not_3 (not_3_out, fAI);
  _74LS273 _74ls273_1 (
    .D0(1'b1), .D1(_74ls273_1_q0), .D2(_74ls273_1_q1), .D3(_74ls273_1_q2), .D4(1'b1), .D5(1'b1), .D6(1'b1),
    .D7(1'b1), .CP(and_1_out), .nMR(not_2_out), .Q0(_74ls273_1_q0), .Q1(_74ls273_1_q1), .Q2(_74ls273_1_q2),
    .Q3(_74ls273_1_q3));  // open: Q4, Q5, Q6, Q7
  not not_4 (not_4_out, _74ls273_1_q1);
  not not_5 (not_5_out, _74ls273_1_q2);
  not not_6 (not_6_out, _74ls273_1_q3);
  and and_2 (and_2_out, _74ls273_1_q0, not_4_out);
  and and_3 (P2, _74ls273_1_q1, not_5_out);
  and and_4 (and_4_out, _74ls273_1_q2, not_6_out);
  or or_2 (or_2_out, _74ls273_1_q3, not_3_out);
  and and_5 (Fin, or_2_out, EN);
  or or_3 (or_3_out, and_2_out, P2, and_4_out);
  or or_4 (P1a, or_3_out, or_3_out);
  or or_5 (P1b, or_3_out, or_3_out);
  or or_6 (P3a, and_4_out, and_4_out);
  or or_7 (P3b, and_4_out, and_4_out);

  // Other names for the same wires on the sheet: ckIncDBUS__anditadi = P2; enIncToDBUS_anditadi = P3b;
  //   enINSTRtoABUS_andtad = P1b; enRAMtoDBUS_andtad = P1a; weRAM_anditadi = P3a
endmodule
