// Digital circuit TTY.dig as structural Verilog
module TTY (
  input  ck,
  input  [11:0] Tx,
  input  TxTrig,
  input  RxAck,
  input  RxEn,
  output TxDone,
  output [11:0] Rx,
  output RxAvail
);

  wire and_1_out, d_ff_as_1_q, d_ff_as_2_q, d_ff_as_3_q, d_ff_as_4_q, d_ff_as_5_q, or_1_out, or_2_out,
       rs_ff_as_1_q;
  wire [7:7] telnet_1_out;

  RS_FF_AS rs_ff_as_1 (.S(TxTrig), .R(1'b0), .Q(rs_ff_as_1_q));  // open: nQ
  and and_1 (and_1_out, ck, rs_ff_as_1_q);
  D_FF_AS d_ff_as_1 (.Set(1'b0), .D(1'b1), .C(and_1_out), .Clr(TxTrig), .Q(d_ff_as_1_q));  // open: nQ
  or or_1 (or_1_out, TxTrig, RxAck);
  or or_2 (or_2_out, RxAck, RxEn);
  D_FF_AS d_ff_as_2 (.Set(1'b0), .D(d_ff_as_1_q), .C(and_1_out), .Clr(TxTrig), .Q(d_ff_as_2_q));  // open: nQ
  D_FF_AS d_ff_as_3 (.Set(1'b0), .D(d_ff_as_2_q), .C(and_1_out), .Clr(TxTrig), .Q(d_ff_as_3_q));  // open: nQ
  D_FF_AS d_ff_as_4 (.Set(1'b0), .D(d_ff_as_3_q), .C(and_1_out), .Clr(TxTrig), .Q(d_ff_as_4_q));  // open: nQ
  D_FF_AS d_ff_as_5 (.Set(1'b0), .D(d_ff_as_4_q), .C(and_1_out), .Clr(TxTrig), .Q(d_ff_as_5_q));  // open: nQ
  Telnet #(.telnetEscape("false")) telnet_1 (
    .in({1'b0, Tx[6:0]}), .C(or_1_out), .wr(TxTrig), .rd(or_2_out), .out({telnet_1_out[7], Rx[6:0]}),
    .av(RxAvail));
  OneShot oneshot_1 (.i(d_ff_as_5_q), .o(TxDone));
  assign Rx[7] = or_2_out ? 1'b1 : 1'bz;  // Driver driver_1
  assign Rx[11:8] = or_2_out ? 4'b0000 : 4'bz;  // Driver driver_2

  // Notes on the sheet:
  //   ck: Hz: 25
endmodule
